// Logisim project display_controller_v2.circ as structural Verilog: 4 circuits, main circuit main
module main (
);

  Button RST ();  // open: out
  model8 model8_1 ();  // open: CAR_COL, OBS_COL, OBS_ROW, RST, ROW_ADDR, COL_DATA
  model3 model3_1 ();  // open: LEFT, RIGHT, car_pos
  model4 model4_1 ();  // open: OBS_COL, OBS_ROW, AT_BOTTOM
  // DotMatrix #(.inputtype("select"), .matrixcols(16), .matrixrows(16)) dotmatrix_1: pin names not known
endmodule

module model3 (
  input  LEFT,
  input  RIGHT,
  output [3:0] car_pos
);
endmodule

module model4 (
  output [3:0] OBS_COL,
  output [3:0] OBS_ROW,
  output AT_BOTTOM
);
endmodule

module model8 (
  input  [3:0] CAR_COL,
  input  [3:0] OBS_COL,
  input  [3:0] OBS_ROW,
  input  RST,
  output [3:0] ROW_ADDR,
  output [15:0] COL_DATA
);

  wire clock_1_out, comparator_1_p2, comparator_2_p3, decoder_1_p3, decoder_1_p4, decoder_1_p5,
       decoder_2_out0, decoder_2_out1, decoder_2_out2, decoder_2_out3, decoder_2_out4, decoder_2_out5,
       decoder_2_out6, decoder_2_out7, decoder_2_out8, decoder_2_out9, decoder_2_out10, decoder_2_out11,
       decoder_2_out12, multiplexer_1_p3, multiplexer_1_p4, multiplexer_2_p3, multiplexer_2_p4, SCAN_ROW_p3;

  Clock clock_1 (.out(clock_1_out));
  // Register #(.width(4)) SCAN_ROW: pin names not known; wires that end beside it: clock_1_out, RST, SCAN_ROW_p3
  // Decoder #(.select(4)) decoder_1: pin names not known; wires that end beside it: SCAN_ROW_p3, CAR_COL, decoder_1_p3, decoder_1_p4, decoder_1_p5
  Decoder #(.select(4)) decoder_2 (
    .out0(decoder_2_out0), .out1(decoder_2_out1), .out2(decoder_2_out2), .out3(decoder_2_out3),
    .out4(decoder_2_out4), .out5(decoder_2_out5), .out6(decoder_2_out6), .out7(decoder_2_out7),
    .out8(decoder_2_out8), .out9(decoder_2_out9), .out10(decoder_2_out10), .out11(decoder_2_out11),
    .out12(decoder_2_out12));  // open: out13, out14, out15, sel, en
  // Adder #(.width(4)) adder_1: pin names not known; wires that end beside it: 4'b1111, 4'b0001, SCAN_ROW_p3
  // Comparator #(.width(4)) comparator_1: pin names not known; wires that end beside it: 4'b1111, comparator_1_p2
  // Comparator #(.width(4)) comparator_2: pin names not known; wires that end beside it: 4'b1111, OBS_ROW, comparator_2_p3
  // Multiplexer #(.width(16)) multiplexer_1: pin names not known; wires that end beside it: comparator_1_p2, 16'h1, multiplexer_1_p3, multiplexer_1_p4
  // Multiplexer #(.width(16)) multiplexer_2: pin names not known; wires that end beside it: comparator_2_p3, 16'h1, multiplexer_2_p3, multiplexer_2_p4
  // OR_Gate #(.width(16)) or_1: pin names not known; wires that end beside it: multiplexer_2_p4, multiplexer_1_p4, COL_DATA

  assign ROW_ADDR = 4'b1111;
endmodule
