// Logisim project Example15_FlipFlopEn.circ as structural Verilog: 9 circuits, main circuit main
module main (
  input  in_1,
  input  in_2,
  input  in_3,
  input  in_4,
  input  [3:0] Test,
  input  in_6,
  input  in_7,
  input  in_8,
  input  in_9,
  input  B,
  input  A,
  input  C,
  output Y
);

  wire and_1_out, and_2_out;

  Hex_Digit_Display hex_digit_display_1 (.value(Test));  // open: dp
  and and_1 (and_1_out, B, A);
  and and_2 (and_2_out, A, C);
  _7_Segment_Display u_7_segment_display_1 (
    .g(in_1), .f(in_2), .a(in_3), .b(in_4), .e(in_6), .d(in_7), .c(in_8), .dp(in_9));
  or or_1 (Y, and_1_out, and_2_out);
endmodule

module SRLatch (
  input  R,
  input  Set,
  output Q,
  output Q_bar
);

  nor nor_1 (Q, R, Q_bar);
  nor nor_2 (Q_bar, Q, Set);
endmodule

module DLatch (
  input  CLK,
  input  Data,
  output Q,
  output Q_bar
);

  wire and_1_out, and_2_out, not_1_out;

  not not_1 (not_1_out, Data);
  and and_1 (and_1_out, CLK, not_1_out);
  and and_2 (and_2_out, CLK, Data);
  LED led_1 (.in(Q));
  SRLatch srlatch_1 (.R(and_1_out), .Set(and_2_out), .Q(Q), .Q_bar(Q_bar));
endmodule

module DFlipFlop (
  input  CLK,
  input  Data,
  output Q,
  output Q_bar
);

  wire dlatch_1_q, not_1_out;

  not not_1 (not_1_out, CLK);
  DLatch dlatch_1 (.CLK(not_1_out), .Data(Data), .Q(dlatch_1_q));  // open: Q_bar
  DLatch dlatch_2 (.CLK(CLK), .Data(dlatch_1_q), .Q(Q), .Q_bar(Q_bar));

  // Notes on the sheet:
  //   主
  //   从
endmodule

module FourBitRegister (
  input  CLK,
  input  [3:0] Data,
  output [3:0] Q
);

  DFlipFlop dflipflop_1 (.CLK(CLK), .Data(Data[0]), .Q(Q[0]));  // open: Q_bar
  DFlipFlop dflipflop_2 (.CLK(CLK), .Data(Data[1]), .Q(Q[1]));  // open: Q_bar
  DFlipFlop dflipflop_3 (.CLK(CLK), .Data(Data[2]), .Q(Q[2]));  // open: Q_bar
  DFlipFlop dflipflop_4 (.CLK(CLK), .Data(Data[3]), .Q(Q[3]));  // open: Q_bar
endmodule

module ShiftRegister (
  input  Din
);

  wire CLK_out, dflipflop_1_q, dflipflop_2_q, dflipflop_3_q, dflipflop_4_q;

  Clock CLK (.out(CLK_out));
  DFlipFlop dflipflop_1 (.CLK(CLK_out), .Data(Din), .Q(dflipflop_1_q));  // open: Q_bar
  DFlipFlop dflipflop_2 (.CLK(CLK_out), .Data(dflipflop_1_q), .Q(dflipflop_2_q));  // open: Q_bar
  DFlipFlop dflipflop_3 (.CLK(CLK_out), .Data(dflipflop_2_q), .Q(dflipflop_3_q));  // open: Q_bar
  DFlipFlop dflipflop_4 (.CLK(CLK_out), .Data(dflipflop_3_q), .Q(dflipflop_4_q));  // open: Q_bar
  LED led_1 (.in(dflipflop_1_q));
  LED led_2 (.in(dflipflop_2_q));
  LED led_3 (.in(dflipflop_3_q));
  LED led_4 (.in(dflipflop_4_q));
endmodule

module FlipFlopEn (
  input  CLK,
  input  Data,
  input  Enable,
  output Q
);

  wire multiplexer_1_out;

  Multiplexer multiplexer_1 (.in0(Q), .in1(Data), .out(multiplexer_1_out), .sel(Enable));
  DFlipFlop dflipflop_1 (.CLK(CLK), .Data(multiplexer_1_out), .Q(Q));  // open: Q_bar
endmodule

module FlipFlopReset (
  input  CLK,
  input  Data,
  input  Reset,
  output Q,
  output Q_bar
);

  wire and_1_out, not_1_out;

  not not_1 (not_1_out, Reset);
  and and_1 (and_1_out, Data, not_1_out);
  DFlipFlop dflipflop_1 (.CLK(CLK), .Data(and_1_out), .Q(Q), .Q_bar(Q_bar));

  // Notes on the sheet:
  //   带复位端的D触发器（高电平复位）
endmodule

module ShiftRegister_Set (
  input  Din,
  input  in_2,
  input  in_3,
  input  in_4,
  input  in_5
);

  wire button_1_out, CLK_out, dflipflop_1_q, dflipflop_2_q, dflipflop_3_q, dflipflop_4_q, multiplexer_1_out,
       multiplexer_2_out, multiplexer_3_out, multiplexer_4_out;

  Button button_1 (.out(button_1_out));
  Multiplexer multiplexer_1 (.in0(Din), .in1(in_2), .out(multiplexer_1_out), .sel(button_1_out));
  Multiplexer multiplexer_2 (.in0(dflipflop_1_q), .in1(in_3), .out(multiplexer_2_out), .sel(button_1_out));
  Multiplexer multiplexer_3 (.in0(dflipflop_2_q), .in1(in_4), .out(multiplexer_3_out), .sel(button_1_out));
  Multiplexer multiplexer_4 (.in0(dflipflop_3_q), .in1(in_5), .out(multiplexer_4_out), .sel(button_1_out));
  Clock CLK (.out(CLK_out));
  DFlipFlop dflipflop_1 (.CLK(CLK_out), .Data(multiplexer_1_out), .Q(dflipflop_1_q));  // open: Q_bar
  DFlipFlop dflipflop_2 (.CLK(CLK_out), .Data(multiplexer_2_out), .Q(dflipflop_2_q));  // open: Q_bar
  DFlipFlop dflipflop_3 (.CLK(CLK_out), .Data(multiplexer_3_out), .Q(dflipflop_3_q));  // open: Q_bar
  DFlipFlop dflipflop_4 (.CLK(CLK_out), .Data(multiplexer_4_out), .Q(dflipflop_4_q));  // open: Q_bar
  LED led_1 (.in(dflipflop_1_q));
  LED led_2 (.in(dflipflop_2_q));
  LED led_3 (.in(dflipflop_3_q));
  LED led_4 (.in(dflipflop_4_q));
endmodule
