// Logisim project Example18_Counter.circ as structural Verilog
module SRLatch (
  input  Reset,
  input  Set,
  output Q,
  output Q_bar
);

  nor nor_1 (Q, Reset, Q_bar);
  nor nor_2 (Q_bar, Q, Set);
endmodule

module DLatch (
  input  CLK,
  input  Data,
  output Q,
  output Q_bar
);

  wire and_1_out, and_2_out, not_1_out;

  not not_1 (not_1_out, Data);
  and and_1 (and_1_out, CLK, not_1_out);
  and and_2 (and_2_out, CLK, Data);
  SRLatch srlatch_1 (.Reset(and_1_out), .Set(and_2_out), .Q(Q), .Q_bar(Q_bar));
endmodule

module DFlipFlop (
  input  CLK,
  input  Data,
  output Q,
  output Q_bar
);

  wire dlatch_1_q, not_1_out;

  not not_1 (not_1_out, CLK);
  DLatch dlatch_1 (.CLK(not_1_out), .Data(Data), .Q(dlatch_1_q));  // open: Q_bar
  DLatch dlatch_2 (.CLK(CLK), .Data(dlatch_1_q), .Q(Q), .Q_bar(Q_bar));

  // Notes on the sheet:
  //   主
  //   从
endmodule

module FourBitRegister (
  input  CLK,
  input  [3:0] Data,
  output [3:0] Q
);

  DFlipFlop dflipflop_1 (.CLK(CLK), .Data(Data[0]), .Q(Q[0]));  // open: Q_bar
  DFlipFlop dflipflop_2 (.CLK(CLK), .Data(Data[1]), .Q(Q[1]));  // open: Q_bar
  DFlipFlop dflipflop_3 (.CLK(CLK), .Data(Data[2]), .Q_bar(Q[2]));  // open: Q
  DFlipFlop dflipflop_4 (.CLK(CLK), .Data(Data[3]), .Q(Q[3]));  // open: Q_bar
endmodule

module ShiftRegister (
  input  Din
);

  wire CLK_out, dflipflop_1_q, dflipflop_2_q, dflipflop_3_q, dflipflop_4_q;

  Clock CLK (.out(CLK_out));
  DFlipFlop dflipflop_1 (.CLK(CLK_out), .Data(Din), .Q(dflipflop_1_q));  // open: Q_bar
  DFlipFlop dflipflop_2 (.CLK(CLK_out), .Data(dflipflop_1_q), .Q(dflipflop_2_q));  // open: Q_bar
  DFlipFlop dflipflop_3 (.CLK(CLK_out), .Data(dflipflop_2_q), .Q(dflipflop_3_q));  // open: Q_bar
  DFlipFlop dflipflop_4 (.CLK(CLK_out), .Data(dflipflop_3_q), .Q(dflipflop_4_q));  // open: Q_bar
  LED led_1 (.in(dflipflop_1_q));
  LED led_2 (.in(dflipflop_2_q));
  LED led_3 (.in(dflipflop_3_q));
  LED led_4 (.in(dflipflop_4_q));
endmodule

module FlipFlopEn (
  input  CLK,
  input  Data,
  input  Enable,
  output Q
);

  wire multiplexer_1_out;

  Multiplexer multiplexer_1 (.in0(Q), .in1(Data), .out(multiplexer_1_out), .sel(Enable));
  DFlipFlop dflipflop_1 (.CLK(CLK), .Data(multiplexer_1_out), .Q(Q));  // open: Q_bar
endmodule

module Decoder2to4 (
  input  [1:0] addr,
  output y0,
  output y1,
  output y2,
  output y3
);

  wire not_1_out, not_2_out;

  not not_1 (not_1_out, addr[1]);
  not not_2 (not_2_out, addr[0]);
  and and_1 (y0, not_1_out, not_2_out);
  and and_2 (y1, not_1_out, addr[0]);
  and and_3 (y2, addr[1], not_2_out);
  and and_4 (y3, addr[1], addr[0]);
endmodule

module FlipFlopEnBuf (
  input  CLK,
  input  Data,
  input  Write_En,
  input  Read_En,
  output Q
);

  wire dflipflop_1_q, multiplexer_1_out;

  Multiplexer multiplexer_1 (.in0(dflipflop_1_q), .in1(Data), .out(multiplexer_1_out), .sel(Write_En));
  DFlipFlop dflipflop_1 (.CLK(CLK), .Data(multiplexer_1_out), .Q(dflipflop_1_q));  // open: Q_bar
  assign Q = Read_En ? dflipflop_1_q : 1'bz;  // Controlled_Buffer controlled_buffer_1
endmodule

module MemoryArray4x2 (
  input  [1:0] WriteData,
  input  [1:0] WriteAddr,
  input  [1:0] ReadAddr,
  output [1:0] ReadData
);

  wire CLK_out, decoder2to4_1_y0, decoder2to4_1_y1, decoder2to4_1_y2, decoder2to4_1_y3, decoder2to4_2_y0,
       decoder2to4_2_y1, decoder2to4_2_y2, decoder2to4_2_y3;

  Clock CLK (.out(CLK_out));
  Decoder2to4 decoder2to4_1 (
    .addr(WriteAddr), .y0(decoder2to4_1_y0), .y1(decoder2to4_1_y1), .y2(decoder2to4_1_y2),
    .y3(decoder2to4_1_y3));
  Decoder2to4 decoder2to4_2 (
    .addr(ReadAddr), .y0(decoder2to4_2_y0), .y1(decoder2to4_2_y1), .y2(decoder2to4_2_y2),
    .y3(decoder2to4_2_y3));
  FlipFlopEnBuf flipflopenbuf_1 (
    .CLK(CLK_out), .Data(WriteData[1]), .Write_En(decoder2to4_1_y0), .Read_En(decoder2to4_2_y0),
    .Q(ReadData[1]));
  FlipFlopEnBuf flipflopenbuf_2 (
    .CLK(CLK_out), .Data(WriteData[1]), .Write_En(decoder2to4_1_y1), .Read_En(decoder2to4_2_y1),
    .Q(ReadData[1]));
  FlipFlopEnBuf flipflopenbuf_3 (
    .CLK(CLK_out), .Data(WriteData[1]), .Write_En(decoder2to4_1_y2), .Read_En(decoder2to4_2_y2),
    .Q(ReadData[1]));
  FlipFlopEnBuf flipflopenbuf_4 (
    .CLK(CLK_out), .Data(WriteData[1]), .Write_En(decoder2to4_1_y3), .Read_En(decoder2to4_2_y3),
    .Q(ReadData[1]));
  FlipFlopEnBuf flipflopenbuf_5 (
    .CLK(CLK_out), .Data(WriteData[0]), .Write_En(decoder2to4_1_y0), .Read_En(decoder2to4_2_y0),
    .Q(ReadData[0]));
  FlipFlopEnBuf flipflopenbuf_6 (
    .CLK(CLK_out), .Data(WriteData[0]), .Write_En(decoder2to4_1_y1), .Read_En(decoder2to4_2_y1),
    .Q(ReadData[0]));
  FlipFlopEnBuf flipflopenbuf_7 (
    .CLK(CLK_out), .Data(WriteData[0]), .Write_En(decoder2to4_1_y2), .Read_En(decoder2to4_2_y2),
    .Q(ReadData[0]));
  FlipFlopEnBuf flipflopenbuf_8 (
    .CLK(CLK_out), .Data(WriteData[0]), .Write_En(decoder2to4_1_y3), .Read_En(decoder2to4_2_y3),
    .Q(ReadData[0]));

  // Notes on the sheet:
  //   WrteData[0]
  //   WrteData[1]
  //   写地址2:4译码器
  //   读地址2:4译码器
  //   D1
  //   D0
  //   地址00对应的字
  //   地址01对应的字
  //   地址10对应的字
  //   地址11对应的字
endmodule

module FlipFlopReset (
  input  CLK,
  input  Data,
  input  Reset,
  output Q,
  output Q_bar
);

  wire and_1_out, not_1_out;

  and and_1 (and_1_out, Data, not_1_out);
  not not_1 (not_1_out, Reset);
  DFlipFlop dflipflop_1 (.CLK(CLK), .Data(and_1_out), .Q(Q), .Q_bar(Q_bar));

  // Notes on the sheet:
  //   带复位端的D触发器（高电平复位）
endmodule

module Conflict_Example (
  input  in_1,
  input  in_2,
  output out_3,
  output out_4
);

  wire d_ff_3_q, d_ff_4_q;

  D_Flip_Flop d_ff_1 (.Q(out_3));  // open: D, clk, Qn, preset, reset
  D_Flip_Flop d_ff_2 (.Q(out_3));  // open: D, clk, Qn, preset, reset
  D_Flip_Flop d_ff_3 (.Q(d_ff_3_q));  // open: D, clk, Qn, preset, reset
  D_Flip_Flop d_ff_4 (.Q(d_ff_4_q));  // open: D, clk, Qn, preset, reset
  assign out_4 = in_1 ? d_ff_3_q : 1'bz;  // Controlled_Buffer controlled_buffer_1
  assign out_4 = in_2 ? d_ff_4_q : 1'bz;  // Controlled_Buffer controlled_buffer_2

  // Notes on the sheet:
  //   多个输出连到同一个输入，造成冲突
  //   通过三态缓冲器，消除冲突
endmodule

module Counter_Simple (
);

  wire clock_1_out;
  wire [3:0] adder_1_out, register_1_q;

  Clock clock_1 (.out(clock_1_out));
  Adder #(.width(4)) adder_1 (.a(register_1_q), .b(4'b0001), .out(adder_1_out));  // open: cin, cout
  Register #(.width(4)) register_1 (.D(adder_1_out), .clk(clock_1_out), .Q(register_1_q));  // open: en, clr
  Hex_Digit_Display hex_digit_display_1 (.value(adder_1_out));  // open: dp
  Hex_Digit_Display hex_digit_display_2 (.value(register_1_q));  // open: dp

  // Notes on the sheet:
  //   1、介绍常量，如何修改（回车）
  //   5、介绍鼠标停留读端口信息
  //   7、介绍仿真后，怎么看时序图/波形图
  //   4比特加法器
  //   2、介绍时钟、频率；介绍怎么把模块符号变小
  //   4、介绍重置仿真：软件使用出现问题时，“模拟”-->“重置仿真”
  //   6、上面模块有些信号未连接，应该怎么做？
  //   4比特寄存器
  //   3、介绍连线的不同颜色：浅绿（1）、深绿（0）、橙色（位宽不匹配）、红色（冲突）、蓝线（有问题，重置仿真）
endmodule

module Counter_Bounded (
  input  [3:0] in_1,
  output [3:0] Result
);

  wire clock_1_out, comparator_1_eq;
  wire [3:0] adder_1_out, multiplexer_1_out;

  Adder #(.width(4)) adder_1 (.a(Result), .b(4'b0001), .out(adder_1_out));  // open: cin, cout
  Comparator #(.width(4)) comparator_1 (.a(Result), .b(in_1), .eq(comparator_1_eq));  // open: gt, lt
  Register #(.width(4)) register_1 (.D(multiplexer_1_out), .clk(clock_1_out), .Q(Result));  // open: en, clr
  Multiplexer #(.width(4)) multiplexer_1 (
    .in0(adder_1_out), .in1(4'b0000), .out(multiplexer_1_out), .sel(comparator_1_eq));
  Clock clock_1 (.out(clock_1_out));
  Hex_Digit_Display hex_digit_display_1 (.value(Result));  // open: dp

  // Notes on the sheet:
  //   上限值
  //   4、介绍重置仿真
  //   4比特加法器
  //   1、介绍常量，如何修改（回车）
  //   2、介绍时钟、频率；介绍怎么把模块符号变小
  //   5、介绍鼠标停留读端口信息
  //   6、上面模块有些信号未连接，应该怎么做？
  //   7、介绍仿真后，怎么看时序图/波形图
  //   下限值
  //   4比特寄存器
  //   3、介绍连线的不同颜色：浅绿（1）、深绿（0）、橙色（位宽不匹配）、红色（冲突）、蓝线（有问题，重置仿真）
endmodule
