// Logisim project Example19_CoinMachine.circ as structural Verilog
module SRLatch (
  input  Reset,
  input  Set,
  output Q,
  output Q_bar
);

  nor nor_1 (Q, Reset, Q_bar);
  nor nor_2 (Q_bar, Q, Set);
endmodule

module DLatch (
  input  CLK,
  input  Data,
  output Q,
  output Q_bar
);

  wire and_1_out, and_2_out, not_1_out;

  not not_1 (not_1_out, Data);
  and and_1 (and_1_out, CLK, not_1_out);
  and and_2 (and_2_out, CLK, Data);
  SRLatch srlatch_1 (.Reset(and_1_out), .Set(and_2_out), .Q(Q), .Q_bar(Q_bar));
endmodule

module DFlipFlop (
  input  CLK,
  input  Data,
  output Q,
  output Q_bar
);

  wire dlatch_1_q, not_1_out;

  not not_1 (not_1_out, CLK);
  DLatch dlatch_1 (.CLK(not_1_out), .Data(Data), .Q(dlatch_1_q));  // open: Q_bar
  DLatch dlatch_2 (.CLK(CLK), .Data(dlatch_1_q), .Q(Q), .Q_bar(Q_bar));

  // Notes on the sheet:
  //   主
  //   从
endmodule

module FourBitRegister (
  input  CLK,
  input  [3:0] Data,
  output [3:0] Q
);

  DFlipFlop dflipflop_1 (.CLK(CLK), .Data(Data[0]), .Q(Q[0]));  // open: Q_bar
  DFlipFlop dflipflop_2 (.CLK(CLK), .Data(Data[1]), .Q(Q[1]));  // open: Q_bar
  DFlipFlop dflipflop_3 (.CLK(CLK), .Data(Data[2]), .Q_bar(Q[2]));  // open: Q
  DFlipFlop dflipflop_4 (.CLK(CLK), .Data(Data[3]), .Q(Q[3]));  // open: Q_bar
endmodule

module ShiftRegister (
  input  Din
);

  wire CLK_out, dflipflop_1_q, dflipflop_2_q, dflipflop_3_q, dflipflop_4_q;

  Clock CLK (.out(CLK_out));
  DFlipFlop dflipflop_1 (.CLK(CLK_out), .Data(Din), .Q(dflipflop_1_q));  // open: Q_bar
  DFlipFlop dflipflop_2 (.CLK(CLK_out), .Data(dflipflop_1_q), .Q(dflipflop_2_q));  // open: Q_bar
  DFlipFlop dflipflop_3 (.CLK(CLK_out), .Data(dflipflop_2_q), .Q(dflipflop_3_q));  // open: Q_bar
  DFlipFlop dflipflop_4 (.CLK(CLK_out), .Data(dflipflop_3_q), .Q(dflipflop_4_q));  // open: Q_bar
  LED led_1 (.in(dflipflop_1_q));
  LED led_2 (.in(dflipflop_2_q));
  LED led_3 (.in(dflipflop_3_q));
  LED led_4 (.in(dflipflop_4_q));
endmodule

module FlipFlopEn (
  input  CLK,
  input  Data,
  input  Enable,
  output Q
);

  wire multiplexer_1_out;

  Multiplexer multiplexer_1 (.in0(Q), .in1(Data), .out(multiplexer_1_out), .sel(Enable));
  DFlipFlop dflipflop_1 (.CLK(CLK), .Data(multiplexer_1_out), .Q(Q));  // open: Q_bar
endmodule

module Decoder2to4 (
  input  [1:0] addr,
  output y0,
  output y1,
  output y2,
  output y3
);

  wire not_1_out, not_2_out;

  not not_1 (not_1_out, addr[1]);
  not not_2 (not_2_out, addr[0]);
  and and_1 (y0, not_1_out, not_2_out);
  and and_2 (y1, not_1_out, addr[0]);
  and and_3 (y2, addr[1], not_2_out);
  and and_4 (y3, addr[1], addr[0]);
endmodule

module FlipFlopEnBuf (
  input  CLK,
  input  Data,
  input  Write_En,
  input  Read_En,
  output Q
);

  wire dflipflop_1_q, multiplexer_1_out;

  Multiplexer multiplexer_1 (.in0(dflipflop_1_q), .in1(Data), .out(multiplexer_1_out), .sel(Write_En));
  DFlipFlop dflipflop_1 (.CLK(CLK), .Data(multiplexer_1_out), .Q(dflipflop_1_q));  // open: Q_bar
  assign Q = Read_En ? dflipflop_1_q : 1'bz;  // Controlled_Buffer controlled_buffer_1
endmodule

module MemoryArray4x2 (
  input  [1:0] WriteData,
  input  [1:0] WriteAddr,
  input  [1:0] ReadAddr,
  output [1:0] ReadData
);

  wire CLK_out, decoder2to4_1_y0, decoder2to4_1_y1, decoder2to4_1_y2, decoder2to4_1_y3, decoder2to4_2_y0,
       decoder2to4_2_y1, decoder2to4_2_y2, decoder2to4_2_y3;

  Clock CLK (.out(CLK_out));
  Decoder2to4 decoder2to4_1 (
    .addr(WriteAddr), .y0(decoder2to4_1_y0), .y1(decoder2to4_1_y1), .y2(decoder2to4_1_y2),
    .y3(decoder2to4_1_y3));
  Decoder2to4 decoder2to4_2 (
    .addr(ReadAddr), .y0(decoder2to4_2_y0), .y1(decoder2to4_2_y1), .y2(decoder2to4_2_y2),
    .y3(decoder2to4_2_y3));
  FlipFlopEnBuf flipflopenbuf_1 (
    .CLK(CLK_out), .Data(WriteData[1]), .Write_En(decoder2to4_1_y0), .Read_En(decoder2to4_2_y0),
    .Q(ReadData[1]));
  FlipFlopEnBuf flipflopenbuf_2 (
    .CLK(CLK_out), .Data(WriteData[1]), .Write_En(decoder2to4_1_y1), .Read_En(decoder2to4_2_y1),
    .Q(ReadData[1]));
  FlipFlopEnBuf flipflopenbuf_3 (
    .CLK(CLK_out), .Data(WriteData[1]), .Write_En(decoder2to4_1_y2), .Read_En(decoder2to4_2_y2),
    .Q(ReadData[1]));
  FlipFlopEnBuf flipflopenbuf_4 (
    .CLK(CLK_out), .Data(WriteData[1]), .Write_En(decoder2to4_1_y3), .Read_En(decoder2to4_2_y3),
    .Q(ReadData[1]));
  FlipFlopEnBuf flipflopenbuf_5 (
    .CLK(CLK_out), .Data(WriteData[0]), .Write_En(decoder2to4_1_y0), .Read_En(decoder2to4_2_y0),
    .Q(ReadData[0]));
  FlipFlopEnBuf flipflopenbuf_6 (
    .CLK(CLK_out), .Data(WriteData[0]), .Write_En(decoder2to4_1_y1), .Read_En(decoder2to4_2_y1),
    .Q(ReadData[0]));
  FlipFlopEnBuf flipflopenbuf_7 (
    .CLK(CLK_out), .Data(WriteData[0]), .Write_En(decoder2to4_1_y2), .Read_En(decoder2to4_2_y2),
    .Q(ReadData[0]));
  FlipFlopEnBuf flipflopenbuf_8 (
    .CLK(CLK_out), .Data(WriteData[0]), .Write_En(decoder2to4_1_y3), .Read_En(decoder2to4_2_y3),
    .Q(ReadData[0]));

  // Notes on the sheet:
  //   WrteData[0]
  //   WrteData[1]
  //   写地址2:4译码器
  //   读地址2:4译码器
  //   D1
  //   D0
  //   地址00对应的字
  //   地址01对应的字
  //   地址10对应的字
  //   地址11对应的字
endmodule

module FlipFlopReset (
  input  CLK,
  input  Data,
  input  Reset,
  output Q,
  output Q_bar
);

  wire and_1_out, not_1_out;

  and and_1 (and_1_out, Data, not_1_out);
  not not_1 (not_1_out, Reset);
  DFlipFlop dflipflop_1 (.CLK(CLK), .Data(and_1_out), .Q(Q), .Q_bar(Q_bar));

  // Notes on the sheet:
  //   带复位端的D触发器（高电平复位）
endmodule

module Conflict_Example (
  input  in_1,
  input  in_2,
  output out_3,
  output out_4
);

  wire d_ff_3_q, d_ff_4_q;

  D_Flip_Flop d_ff_1 (.Q(out_3));  // open: D, clk, Qn, preset, reset
  D_Flip_Flop d_ff_2 (.Q(out_3));  // open: D, clk, Qn, preset, reset
  D_Flip_Flop d_ff_3 (.Q(d_ff_3_q));  // open: D, clk, Qn, preset, reset
  D_Flip_Flop d_ff_4 (.Q(d_ff_4_q));  // open: D, clk, Qn, preset, reset
  assign out_4 = in_1 ? d_ff_3_q : 1'bz;  // Controlled_Buffer controlled_buffer_1
  assign out_4 = in_2 ? d_ff_4_q : 1'bz;  // Controlled_Buffer controlled_buffer_2

  // Notes on the sheet:
  //   多个输出连到同一个输入，造成冲突
  //   通过三态缓冲器，消除冲突
endmodule

module Counter_Simple (
);

  wire clock_1_out;
  wire [3:0] adder_1_out, register_1_q;

  Clock clock_1 (.out(clock_1_out));
  Adder #(.width(4)) adder_1 (.a(register_1_q), .b(4'b0001), .out(adder_1_out));  // open: cin, cout
  Register #(.width(4)) register_1 (.D(adder_1_out), .clk(clock_1_out), .Q(register_1_q));  // open: en, clr
  Hex_Digit_Display hex_digit_display_1 (.value(adder_1_out));  // open: dp
  Hex_Digit_Display hex_digit_display_2 (.value(register_1_q));  // open: dp

  // Notes on the sheet:
  //   4、介绍重置仿真
  //   1、介绍常量，如何修改（回车）
  //   5、介绍鼠标停留读端口信息
  //   7、介绍仿真后，怎么看时序图/波形图
  //   4比特加法器
  //   2、介绍时钟、频率；介绍怎么把模块符号变小
  //   6、上面模块有些信号未连接，应该怎么做？
  //   4比特寄存器
  //   3、介绍连线的不同颜色：浅绿（1）、深绿（0）、橙色（位宽不匹配）、红色（冲突）、蓝线（有问题，重置仿真）
endmodule

module Counter_Bounded (
  input  [3:0] in_1,
  input  Reset,
  output [3:0] Result
);

  wire clock_1_out, comparator_1_eq;
  wire [3:0] adder_1_out, multiplexer_1_out;

  Adder #(.width(4)) adder_1 (.a(Result), .b(4'b0001), .out(adder_1_out));  // open: cin, cout
  Comparator #(.width(4)) comparator_1 (.a(Result), .b(in_1), .eq(comparator_1_eq));  // open: gt, lt
  Register #(.width(4)) register_1 (.D(multiplexer_1_out), .clk(clock_1_out), .Q(Result), .clr(Reset));  // open: en
  Multiplexer #(.width(4)) multiplexer_1 (
    .in0(adder_1_out), .in1(4'b0000), .out(multiplexer_1_out), .sel(comparator_1_eq));
  Clock clock_1 (.out(clock_1_out));
  Hex_Digit_Display hex_digit_display_1 (.value(Result));  // open: dp

  // Notes on the sheet:
  //   上限值
  //   4、介绍重置仿真
  //   4比特加法器
  //   1、介绍常量，如何修改（回车）
  //   2、介绍时钟、频率；介绍怎么把模块符号变小
  //   5、介绍鼠标停留读端口信息
  //   6、上面模块有些信号未连接，应该怎么做？
  //   7、介绍仿真后，怎么看时序图/波形图
  //   下限值
  //   4比特寄存器
  //   3、介绍连线的不同颜色：浅绿（1）、深绿（0）、橙色（位宽不匹配）、红色（冲突）、蓝线（有问题，重置仿真）
endmodule

module CoinMachine_1 (
  input  Reset
);

  wire button_1_out, clock_1_out, comparator_1_eq;
  wire [3:0] adder_1_out, multiplexer_1_out, multiplexer_2_out, register_1_q;

  Multiplexer #(.width(4)) multiplexer_1 (.in0(4'b0000), .in1(4'b0101), .out(multiplexer_1_out), .sel(button_1_out));
  Button button_1 (.out(button_1_out));
  Adder #(.width(4)) adder_1 (.a(register_1_q), .b(multiplexer_1_out), .out(adder_1_out));  // open: cin, cout
  Comparator #(.width(4)) comparator_1 (.a(register_1_q), .b(4'b1010), .eq(comparator_1_eq));  // open: gt, lt
  Multiplexer #(.width(4)) multiplexer_2 (
    .in0(adder_1_out), .in1(4'b0000), .out(multiplexer_2_out), .sel(comparator_1_eq));
  LED led_1 (.in(comparator_1_eq));
  Register #(.width(4)) register_1 (
    .D(multiplexer_2_out), .clk(clock_1_out), .Q(register_1_q), .clr(Reset));  // open: en
  Clock clock_1 (.out(clock_1_out));
  Hex_Digit_Display hex_digit_display_1 (.value(register_1_q));  // open: dp

  // Notes on the sheet:
  //   设计方案1：基于加法器，每投递5元累加5
  //   投币按钮
  //   上限值
  //   4比特加法器
  //   下限值
  //   比较器
  //   场景描述：投币机只接受5元面额的纸币，且累积达到10元后，系统做出一个特别的响应
  //   累计到10元后，触发售卖、抓娃娃等操作
  //   4比特寄存器
endmodule

module CoinMachine_2 (
  input  Reset
);

  wire button_1_out, clock_1_out, comparator_1_eq;
  wire [1:0] adder_1_out, multiplexer_1_out, multiplexer_2_out, register_1_q;

  Multiplexer #(.width(2)) multiplexer_1 (.in0(2'b00), .in1(2'b01), .out(multiplexer_1_out), .sel(button_1_out));
  Button button_1 (.out(button_1_out));
  Adder #(.width(2)) adder_1 (.a(register_1_q), .b(multiplexer_1_out), .out(adder_1_out));  // open: cin, cout
  Comparator #(.width(2)) comparator_1 (.a(register_1_q), .b(2'b10), .eq(comparator_1_eq));  // open: gt, lt
  Multiplexer #(.width(2)) multiplexer_2 (
    .in0(adder_1_out), .in1(2'b00), .out(multiplexer_2_out), .sel(comparator_1_eq));
  LED led_1 (.in(comparator_1_eq));
  Register #(.width(2)) register_1 (
    .D(multiplexer_2_out), .clk(clock_1_out), .Q(register_1_q), .clr(Reset));  // open: en
  Clock clock_1 (.out(clock_1_out));
  Hex_Digit_Display hex_digit_display_1 (.value({2'b00, register_1_q}));  // open: dp

  // Notes on the sheet:
  //   投币按钮
  //   上限值
  //   2比特加法器
  //   比较器
  //   下限值
  //   累计到2次有效投币后，触发售卖、抓娃娃等操作
  //   场景描述：投币机只接受5元面额的纸币，且累积达到10元后，系统做出一个特别的响应
  //   设计方案2：基于加法器，记录投币的次数，降低各个模块的位宽（从4比特降低为2比特）
  //   2比特寄存器
endmodule

module CoinMachine_3 (
  input  Reset
);

  wire and_1_out, and_2_out, and_3_out, and_4_out, button_1_out, clock_1_out, d_ff_1_q, d_ff_2_q, not_1_out,
       not_2_out, not_3_out, or_1_out;

  Button button_1 (.out(button_1_out));
  not not_1 (not_1_out, d_ff_2_q);
  not not_2 (not_2_out, button_1_out);
  and and_1 (and_1_out, d_ff_2_q, button_1_out);
  and and_2 (and_2_out, not_1_out, button_1_out);
  or or_1 (or_1_out, and_2_out, and_3_out);
  and and_3 (and_3_out, d_ff_2_q, not_2_out);
  Clock clock_1 (.out(clock_1_out));
  D_Flip_Flop d_ff_1 (.D(and_1_out), .clk(clock_1_out), .Q(d_ff_1_q), .reset(Reset));  // open: Qn, preset
  D_Flip_Flop d_ff_2 (.D(or_1_out), .clk(clock_1_out), .Q(d_ff_2_q), .reset(Reset));  // open: Qn, preset
  and and_4 (and_4_out, d_ff_1_q, not_3_out);
  not not_3 (not_3_out, d_ff_2_q);
  LED led_1 (.in(and_4_out));

  // Notes on the sheet:
  //   投币按钮
  //   场景描述：投币机只接受5元面额的纸币，且累积达到10元后，系统做出一个特别的响应
  //   设计方案3：不再基于加法器，而是根据投币系统的状态设计（有限状态机设计法）
  //   系统状态寄存器
  //   S'1
  //   S'0
  //   S1
  //   S0
  //   进入到相应状态后，
  //   触发售卖、抓娃娃等操作
endmodule

module Next_State_Logic (
  input  S1,
  input  S0,
  input  C,
  output S1_next,
  output S0_next
);

  wire and_2_out, and_3_out, not_1_out, not_2_out;

  not not_1 (not_1_out, S0);
  not not_2 (not_2_out, C);
  and and_1 (S1_next, S0, C);
  and and_2 (and_2_out, not_1_out, C);
  and and_3 (and_3_out, S0, not_2_out);
  or or_1 (S0_next, and_2_out, and_3_out);
endmodule

module Output_Logic (
  input  S1,
  input  S0,
  output Y
);


  assign Y = S1;
endmodule

module CoinMachine_3_another (
  input  Reset
);

  wire button_1_out, clock_1_out, d_ff_1_q, d_ff_2_q, next_state_logic_1_s0_next, next_state_logic_1_s1_next,
       output_logic_1_y;

  Button button_1 (.out(button_1_out));
  Next_State_Logic next_state_logic_1 (
    .S1(d_ff_1_q), .S0(d_ff_2_q), .C(button_1_out), .S1_next(next_state_logic_1_s1_next),
    .S0_next(next_state_logic_1_s0_next));
  Clock clock_1 (.out(clock_1_out));
  D_Flip_Flop d_ff_1 (
    .D(next_state_logic_1_s1_next), .clk(clock_1_out), .Q(d_ff_1_q), .reset(Reset));  // open: Qn, preset
  D_Flip_Flop d_ff_2 (
    .D(next_state_logic_1_s0_next), .clk(clock_1_out), .Q(d_ff_2_q), .reset(Reset));  // open: Qn, preset
  Output_Logic output_logic_1 (.S1(d_ff_1_q), .S0(d_ff_2_q), .Y(output_logic_1_y));
  LED led_1 (.in(output_logic_1_y));

  // Notes on the sheet:
  //   投币按钮
  //   场景描述：投币机只接受5元面额的纸币，且累积达到10元后，系统做出一个特别的响应
  //   系统状态寄存器
  //   S'1
  //   S'0
  //   S1
  //   S0
  //   设计方案3（结构化形式）：和设计方案3一样，只是采用了结构化/模块化的方式，将电路分成了“下一状态逻辑”、“系统状态寄存器”、和“输出逻辑”三部分
  //   进入到相应状态后，
  //   触发售卖、抓娃娃等操作
endmodule

module ToothBrush (
  input  Reset
);

  wire and_1_out, and_2_out, and_3_out, and_4_out, and_5_out, and_6_out, clock_1_out, not_1_out, not_2_out,
       not_3_out, not_4_out, not_5_out, or_1_out, or_2_out, P_out, S0_q, S1_q;

  Button P (.out(P_out));
  not not_1 (not_1_out, P_out);
  not not_2 (not_2_out, S1_q);
  not not_3 (not_3_out, S0_q);
  and and_1 (and_1_out, S1_q, not_1_out);
  and and_2 (and_2_out, S0_q, P_out);
  and and_3 (and_3_out, not_1_out, S0_q);
  and and_4 (and_4_out, not_2_out, P_out, not_3_out);
  or or_1 (or_1_out, and_1_out, and_2_out);
  or or_2 (or_2_out, and_3_out, and_4_out);
  Clock clock_1 (.out(clock_1_out));
  D_Flip_Flop S1 (.D(or_1_out), .clk(clock_1_out), .Q(S1_q), .reset(Reset));  // open: Qn, preset
  D_Flip_Flop S0 (.D(or_2_out), .clk(clock_1_out), .Q(S0_q), .reset(Reset));  // open: Qn, preset
  not not_4 (not_4_out, S1_q);
  not not_5 (not_5_out, S0_q);
  LED led_1 (.in(and_5_out));
  and and_5 (and_5_out, S1_q, not_5_out);
  and and_6 (and_6_out, not_4_out, S0_q);
  LED led_2 (.in(and_6_out));

  // Notes on the sheet:
  //   高速模式
  //   标准模式
endmodule
