// Logisim project Example21_FSM_Demo.circ as structural Verilog
module next_state_logic (
  input  s1,
  input  s0,
  input  Ta,
  input  Tb,
  output s1_next,
  output s0_next
);

  wire and_1_out, and_2_out, and_3_out, and_4_out, not_1_out, not_2_out, not_3_out, not_4_out;

  not not_1 (not_1_out, s1);
  not not_2 (not_2_out, s0);
  not not_3 (not_3_out, Ta);
  not not_4 (not_4_out, Tb);
  and and_1 (and_1_out, not_1_out, s0);
  and and_2 (and_2_out, s1, not_2_out);
  and and_3 (and_3_out, not_1_out, not_2_out, not_3_out);
  and and_4 (and_4_out, s1, not_2_out, not_4_out);
  or or_1 (s1_next, and_1_out, and_2_out);
  or or_2 (s0_next, and_3_out, and_4_out);
endmodule

module output_logic (
  input  s1,
  input  s0,
  output Light_A_GRN,
  output Light_A_YLW,
  output Light_A_RED,
  output Light_B_GRN,
  output Light_B_YLW,
  output Light_B_RED
);

  wire not_2_out;

  not not_1 (Light_B_RED, s1);
  not not_2 (not_2_out, s0);
  and and_1 (Light_A_GRN, Light_B_RED, not_2_out);
  and and_2 (Light_A_YLW, Light_B_RED, s0);
  and and_3 (Light_B_GRN, s1, not_2_out);
  and and_4 (Light_B_YLW, s1, s0);

  assign Light_A_RED = s1;
endmodule

module traffic_light_controller (
  input  Reset
);

  wire clock_1_out, next_state_logic_1_s0_next, next_state_logic_1_s1_next, output_logic_1_light_a_grn,
       output_logic_1_light_a_red, output_logic_1_light_a_ylw, output_logic_1_light_b_grn,
       output_logic_1_light_b_red, output_logic_1_light_b_ylw, S0_q, S1_q, Ta_out, Tb_out;

  Button Ta (.out(Ta_out));
  Button Tb (.out(Tb_out));
  Clock clock_1 (.out(clock_1_out));
  next_state_logic next_state_logic_1 (
    .s1(S1_q), .s0(S0_q), .Ta(Ta_out), .Tb(Tb_out), .s1_next(next_state_logic_1_s1_next),
    .s0_next(next_state_logic_1_s0_next));
  D_Flip_Flop S1 (.D(next_state_logic_1_s1_next), .clk(clock_1_out), .Q(S1_q), .reset(Reset));  // open: Qn, preset
  D_Flip_Flop S0 (.D(next_state_logic_1_s0_next), .clk(clock_1_out), .Q(S0_q), .reset(Reset));  // open: Qn, preset
  output_logic output_logic_1 (
    .s1(S1_q), .s0(S0_q), .Light_A_GRN(output_logic_1_light_a_grn), .Light_A_YLW(output_logic_1_light_a_ylw),
    .Light_A_RED(output_logic_1_light_a_red), .Light_B_GRN(output_logic_1_light_b_grn),
    .Light_B_YLW(output_logic_1_light_b_ylw), .Light_B_RED(output_logic_1_light_b_red));
  LED led_1 (.in(output_logic_1_light_a_grn));
  LED led_2 (.in(output_logic_1_light_a_ylw));
  LED led_3 (.in(output_logic_1_light_a_red));
  LED led_4 (.in(output_logic_1_light_b_grn));
  LED led_5 (.in(output_logic_1_light_b_ylw));
  LED led_6 (.in(output_logic_1_light_b_red));

  // Notes on the sheet:
  //   功能描述：
  //   2. 若没有行人请求绿灯，则两个方向周期性地获得亮绿灯的机会
  //   1. 行人使用相应方向的按钮（Ta或Tb）获取绿灯请求，按下后相应方向显示绿灯，另外一个方向显示红灯；
  //   A方向
  //   B方向
endmodule

module long_or_short_press_demo (
  input  Reset,
  output detect_long,
  output detect_short
);

  wire clock_input_out, d_ff_1_q, d_ff_2_q, d_ff_3_q, not_1_out, not_2_out, user_button_out;

  Button user_button (.out(user_button_out));
  Clock clock_input (.out(clock_input_out));
  D_Flip_Flop d_ff_1 (.D(user_button_out), .clk(clock_input_out), .Q(d_ff_1_q), .reset(Reset));  // open: Qn, preset
  D_Flip_Flop d_ff_2 (.D(d_ff_1_q), .clk(clock_input_out), .Q(d_ff_2_q), .reset(Reset));  // open: Qn, preset
  D_Flip_Flop d_ff_3 (.D(d_ff_2_q), .clk(clock_input_out), .Q(d_ff_3_q), .reset(Reset));  // open: Qn, preset
  and and_1 (detect_long, d_ff_1_q, d_ff_2_q, d_ff_3_q);
  not not_1 (not_1_out, d_ff_1_q);
  and and_2 (detect_short, not_1_out, d_ff_2_q, not_2_out);
  not not_2 (not_2_out, d_ff_3_q);
  LED led_1 (.in(detect_long));
  LED led_2 (.in(detect_short));

  // Notes on the sheet:
  //   将检测到的序列"010"定义为一次短按
  //   将检测到的序列"111"定义为一次长按
  //   使用移位寄存器的方式自动采集和保存用户输入的序列
endmodule

module long_or_short_press (
  input  user_input,
  input  clock_input,
  input  Reset,
  output detect_long,
  output detect_short
);

  wire d_ff_1_q, d_ff_2_q, d_ff_3_q, not_1_out, not_2_out;

  D_Flip_Flop d_ff_1 (.D(user_input), .clk(clock_input), .Q(d_ff_1_q), .reset(Reset));  // open: Qn, preset
  D_Flip_Flop d_ff_2 (.D(d_ff_1_q), .clk(clock_input), .Q(d_ff_2_q), .reset(Reset));  // open: Qn, preset
  D_Flip_Flop d_ff_3 (.D(d_ff_2_q), .clk(clock_input), .Q(d_ff_3_q), .reset(Reset));  // open: Qn, preset
  and and_1 (detect_long, d_ff_1_q, d_ff_2_q, d_ff_3_q);
  not not_1 (not_1_out, d_ff_1_q);
  and and_2 (detect_short, not_1_out, d_ff_2_q, not_2_out);
  not not_2 (not_2_out, d_ff_3_q);

  // Notes on the sheet:
  //   将检测到的序列"010"定义为一次短按
  //   将检测到的序列"111"定义为一次长按
  //   使用移位寄存器的方式自动采集和保存用户输入的序列
endmodule

module on_or_off_demo (
  input  Reset,
  output On_or_Off
);

  wire clock_1_out, long_or_short_press_1_detect_short, user_button_out, xor_1_out;

  Button user_button (.out(user_button_out));
  Clock clock_1 (.out(clock_1_out));
  long_or_short_press long_or_short_press_1 (
    .user_input(user_button_out), .clock_input(clock_1_out), .Reset(Reset),
    .detect_short(long_or_short_press_1_detect_short));  // open: detect_long
  LED led_1 (.in(long_or_short_press_1_detect_short));
  xor xor_1 (xor_1_out, On_or_Off, long_or_short_press_1_detect_short);
  D_Flip_Flop d_ff_1 (.D(xor_1_out), .clk(clock_1_out), .Q(On_or_Off), .reset(Reset));  // open: Qn, preset
  LED led_2 (.in(On_or_Off));

  // Notes on the sheet:
  //   系统状态=1时为on，等于0时为off
  //   S'
  //   S
endmodule

module on_or_off (
  input  user_input,
  input  clock_input,
  input  Reset,
  output On_or_Off
);

  wire long_or_short_press_1_detect_short, xor_1_out;

  long_or_short_press long_or_short_press_1 (
    .user_input(user_input), .clock_input(clock_input), .Reset(Reset),
    .detect_short(long_or_short_press_1_detect_short));  // open: detect_long
  LED led_1 (.in(long_or_short_press_1_detect_short));
  D_Flip_Flop d_ff_1 (.D(xor_1_out), .clk(clock_input), .Q(On_or_Off), .reset(Reset));  // open: Qn, preset
  xor xor_1 (xor_1_out, On_or_Off, long_or_short_press_1_detect_short);
  LED led_2 (.in(On_or_Off));

  // Notes on the sheet:
  //   系统状态=1时为on，等于0时为off
  //   S'
  //   S
endmodule

module up_or_down_demo (
  input  Reset,
  output up_or_down,
  output DL_delayed
);

  wire and_1_out, clock_1_out, long_or_short_press_1_detect_long, not_1_out, user_button_out, xor_1_out;

  Button user_button (.out(user_button_out));
  Clock clock_1 (.out(clock_1_out));
  long_or_short_press long_or_short_press_1 (
    .user_input(user_button_out), .clock_input(clock_1_out), .Reset(Reset),
    .detect_long(long_or_short_press_1_detect_long));  // open: detect_short
  not not_1 (not_1_out, long_or_short_press_1_detect_long);
  D_Flip_Flop d_ff_1 (
    .D(long_or_short_press_1_detect_long), .clk(clock_1_out), .Q(DL_delayed), .reset(Reset));  // open: Qn, preset
  and and_1 (and_1_out, not_1_out, DL_delayed);
  LED led_1 (.in(and_1_out));
  xor xor_1 (xor_1_out, up_or_down, and_1_out);
  D_Flip_Flop d_ff_2 (.D(xor_1_out), .clk(clock_1_out), .Q(up_or_down), .reset(Reset));  // open: Qn, preset
  LED led_2 (.in(up_or_down));

  // Notes on the sheet:
  //   系统状态=1时为up（调亮模式），等于0时为down（调暗模式）
  //   DL
  //   T
  //   下一个状态
  //   当前状态
endmodule

module up_or_down (
  input  user_input,
  input  clock_input,
  input  Reset,
  output Up_Down,
  output DL_delayed
);

  wire and_1_out, long_or_short_press_1_detect_long, not_1_out, xor_1_out;

  long_or_short_press long_or_short_press_1 (
    .user_input(user_input), .clock_input(clock_input), .Reset(Reset),
    .detect_long(long_or_short_press_1_detect_long));  // open: detect_short
  not not_1 (not_1_out, long_or_short_press_1_detect_long);
  D_Flip_Flop d_ff_1 (
    .D(long_or_short_press_1_detect_long), .clk(clock_input), .Q(DL_delayed), .reset(Reset));  // open: Qn, preset
  and and_1 (and_1_out, not_1_out, DL_delayed);
  LED led_1 (.in(and_1_out));
  xor xor_1 (xor_1_out, Up_Down, and_1_out);
  D_Flip_Flop d_ff_2 (.D(xor_1_out), .clk(clock_input), .Q(Up_Down), .reset(Reset));  // open: Qn, preset
  LED led_2 (.in(Up_Down));

  // Notes on the sheet:
  //   系统状态=1时为up（调亮模式），等于0时为down（调暗模式）
  //   DL
  //   T
  //   下一个状态
  //   当前状态
endmodule

module lamp_system (
  input  Reset
);

  wire CLK, comparator_1_eq, comparator_2_eq, comparator_3_eq, DL, ON, UP, user_button_out;
  wire [2:0] adder_1_out, multiplexer_1_out, multiplexer_2_out, multiplexer_3_out, multiplexer_4_out,
       multiplexer_5_out, multiplexer_6_out, Q, subtractor_1_out;

  Subtractor #(.width(3)) subtractor_1 (.a(Q), .b(3'b001), .out(subtractor_1_out));  // open: bin, bout
  Adder #(.width(3)) adder_1 (.a(Q), .b(3'b001), .out(adder_1_out));  // open: cin, cout
  Button user_button (.out(user_button_out));
  Clock clock_1 (.out(CLK));
  Comparator #(.mode("unsigned"), .width(3)) comparator_1 (.a(Q), .b(3'b001), .eq(comparator_1_eq));  // open: gt, lt
  Multiplexer #(.width(3)) multiplexer_1 (
    .in0(subtractor_1_out), .in1(Q), .out(multiplexer_1_out), .sel(comparator_1_eq));
  Comparator #(.mode("unsigned"), .width(3)) comparator_2 (.a(Q), .b(3'b100), .eq(comparator_2_eq));  // open: gt, lt
  Multiplexer #(.width(3)) multiplexer_2 (.in0(adder_1_out), .in1(Q), .out(multiplexer_2_out), .sel(comparator_2_eq));
  Multiplexer #(.width(3)) multiplexer_3 (
    .in0(multiplexer_1_out), .in1(multiplexer_2_out), .out(multiplexer_3_out), .sel(UP));
  LED led_1 (.in(ON));
  on_or_off on_or_off_1 (.user_input(user_button_out), .clock_input(CLK), .Reset(Reset), .On_or_Off(ON));
  LED led_2 (.in(UP));
  up_or_down up_or_down_1 (
    .user_input(user_button_out), .clock_input(CLK), .Reset(Reset), .Up_Down(UP), .DL_delayed(DL));
  Multiplexer #(.width(3)) multiplexer_4 (.in0(Q), .in1(multiplexer_3_out), .out(multiplexer_4_out), .sel(DL));
  Comparator #(.mode("unsigned"), .width(3)) comparator_3 (.a(Q), .b(3'b000), .eq(comparator_3_eq));  // open: gt, lt
  Multiplexer #(.width(3)) multiplexer_5 (
    .in0(multiplexer_4_out), .in1(3'b100), .out(multiplexer_5_out), .sel(comparator_3_eq));
  Register #(.width(3)) register_1 (.D(multiplexer_6_out), .clk(CLK), .Q(Q), .clr(Reset));  // open: en
  Multiplexer #(.width(3)) multiplexer_6 (.in0(3'b000), .in1(multiplexer_5_out), .out(multiplexer_6_out), .sel(ON));
  Hex_Digit_Display hex_digit_display_1 (.value({1'b0, Q}));  // open: dp

  // Notes on the sheet:
  //   判断是否已经是最弱亮度
  //   调暗
  //   保持最弱亮度
  //   判断是否已经是最大亮度
  //   调亮
  //   保持最大亮度
  //   用户输入
  //   选择调亮/调暗
  //   调暗
  //   调亮
  //   不调
  //   调亮/调暗
  //   判断是否要调节亮度
  //   调亮/调暗/不调
  //   判断是否首次进入开启
  //   直接进入最大亮度
  //   UP=1时，表示调亮模式；UP=0时，表示调暗模式
  //   DL=1时，表示检测到长按，调节一次亮度
  //   ON=1时，表示台灯处于打开状态；ON=0时，表示台灯处于熄灭状态
  //   熄灭
  //   台灯开启的亮度
  //   台灯开/关控制
  //   台灯亮度值
endmodule
