// Logisim project Example22_long_short_push_LLM.circ as structural Verilog
module sequence_detector_testbench (
  input  in_1,
  input  in_2
);

  wire clock_1_out, sequence_detector_1_long_push, sequence_detector_1_short_push;

  Clock clock_1 (.out(clock_1_out));
  sequence_detector sequence_detector_1 (
    .clk(clock_1_out), .rst_n(in_1), .din(in_2), .short_push(sequence_detector_1_short_push),
    .long_push(sequence_detector_1_long_push));
  LED led_1 (.in(sequence_detector_1_short_push));
  LED led_2 (.in(sequence_detector_1_long_push));

  // Notes on the sheet:
  //   注意：这个设计用的是低电平复位，所以要先将rst_n的输入置为高电平‘1’，退出复位
endmodule

// VHDL entity sequence_detector, as the project stores it:
library IEEE;
use IEEE.STD_LOGIC_1164.ALL;

-- 序列检测模块：检测010(short_push)、111(long_push)
entity sequence_detector is
    Port (
        clk     : in  STD_LOGIC;           -- 时钟信号，周期T
        rst_n   : in  STD_LOGIC;           -- 低电平复位信号
        din     : in  STD_LOGIC;           -- 二进制输入序列
        short_push : out STD_LOGIC;        -- 检测到010输出高
        long_push  : out STD_LOGIC         -- 检测到111输出高
    );
end sequence_detector;

architecture Behavioral of sequence_detector is
    -- 状态定义
    type state_type is (IDLE, S0, S01, S1, S11, S010, S111);
    signal current_state : state_type;  -- 当前状态
    signal next_state    : state_type;  -- 下一个状态

begin

    -- 第一段：时序逻辑，状态寄存器（同步时钟更新）
    process(clk, rst_n)
    begin
        if rst_n = '0' then           -- 异步复位，优先于时钟
            current_state <= IDLE;
        elsif rising_edge(clk) then   -- 时钟上升沿更新状态
            current_state <= next_state;
        end if;
    end process;

    -- 第二段：组合逻辑，状态转移逻辑（根据当前状态+输入决定下一个状态）
    process(current_state, din)
    begin
        case current_state is
            when IDLE =>
                if din = '0' then
                    next_state <= S0;      -- 输入0，进入S0（010起始）
                else
                    next_state <= S1;      -- 输入1，进入S1（111起始）
                end if;

            when S0 =>    -- 已检测到第一个0
                if din = '0' then
                    next_state <= S0;      -- 连续0，保持S0
                else
                    next_state <= S01;     -- 输入1，进入01状态
                end if;

            when S01 =>   -- 已检测到01
                if din = '0' then
                    next_state <= S010;    -- 输入0，检测到010！
                else
                    next_state <= S1;      -- 输入1，跳转到1起始
                end if;

            when S1 =>    -- 已检测到第一个1
                if din = '1' then
                    next_state <= S11;     -- 输入1，进入11状态
                else
                    next_state <= S0;      -- 输入0，跳转到0起始
                end if;

            when S11 =>   -- 已检测到11
                if din = '1' then
                    next_state <= S111;    -- 输入1，检测到111！
                else
                    next_state <= S0;      -- 输入0，跳转到0起始
                end if;

            when S010 =>  -- 检测到010，立即判断下一个输入
                if din = '0' then
                    next_state <= S0;
                else
                    next_state <= S1;
                end if;

            when S111 =>  -- 检测到111，立即判断下一个输入
                if din = '0' then
                    next_state <= S0;
                else
                    next_state <= S111;
                end if;

            when others =>
                next_state <= IDLE;
        end case;
    end process;

    -- 第三段：组合逻辑，输出逻辑（Moore型，只和当前状态相关）
    process(current_state)
    begin
        -- 默认输出低电平
        short_push <= '0';
        long_push  <= '0';
        
        case current_state is
            when S010 =>
                short_push <= '1';   -- 检测到010，输出有效
            when S111 =>
                long_push  <= '1';   -- 检测到111，输出有效
            when others =>
                short_push <= '0';
                long_push  <= '0';
        end case;
    end process;

end Behavioral;
