// Logisim project Example8_AddSubtractor (2).circ as structural Verilog: 9 circuits, main circuit main
module main (
  input  in_1,
  input  [3:0] A,
  input  [3:0] B,
  output [3:0] Result
);

  wire [3:0] fourbitmultiplexer_1_y, not_1_out;

  assign not_1_out = ~B;  // NOT_Gate not_1, 4 bits wide
  FourBitMultiplexer fourbitmultiplexer_1 (.S(in_1), .B(not_1_out), .A(B), .Y(fourbitmultiplexer_1_y));
  FourBitAdder fourbitadder_1 (.Cin(in_1), .A(A), .B(fourbitmultiplexer_1_y), .Sum(Result));  // open: Cout
endmodule

module HalfAdder (
  input  A,
  input  B,
  output Cout,
  output Sum
);

  wire and_2_out, and_3_out, not_1_out, not_2_out;

  not not_1 (not_1_out, A);
  not not_2 (not_2_out, B);
  and and_1 (Cout, A, B);
  and and_2 (and_2_out, not_1_out, B);
  and and_3 (and_3_out, A, not_2_out);
  or or_1 (Sum, and_2_out, and_3_out);
endmodule

module FullAdder (
  input  Cin,
  input  A,
  input  B,
  output Cout,
  output Sum
);

  wire and_1_out, and_2_out, and_3_out, and_4_out, and_5_out, and_6_out, and_7_out, not_1_out, not_2_out,
       not_3_out;

  not not_1 (not_1_out, Cin);
  not not_2 (not_2_out, A);
  not not_3 (not_3_out, B);
  and and_1 (and_1_out, A, B);
  and and_2 (and_2_out, Cin, B);
  and and_3 (and_3_out, Cin, A);
  and and_4 (and_4_out, not_1_out, not_2_out, B);
  and and_5 (and_5_out, not_1_out, A, not_3_out);
  and and_6 (and_6_out, Cin, not_2_out, not_3_out);
  and and_7 (and_7_out, Cin, A, B);
  or or_1 (Cout, and_1_out, and_2_out, and_3_out);
  or or_2 (Sum, and_4_out, and_5_out, and_6_out, and_7_out);
endmodule

module Test (
  input  Cin,
  input  A,
  input  B,
  output Cout,
  output Sum
);

  FullAdder fulladder_1 (.Cin(Cin), .A(A), .B(B), .Cout(Cout), .Sum(Sum));
endmodule

module TwoBitAdder (
  input  Cin,
  input  A0,
  input  B0,
  input  A1,
  input  B1,
  output Sum0,
  output Cout,
  output Sum1
);

  wire fulladder_1_cout;

  FullAdder fulladder_1 (.Cin(Cin), .A(A0), .B(B0), .Cout(fulladder_1_cout), .Sum(Sum0));
  FullAdder fulladder_2 (.Cin(fulladder_1_cout), .A(A1), .B(B1), .Cout(Cout), .Sum(Sum1));

  // Notes on the sheet:
  //   低位加法器
  //   高位加法器
endmodule

module FourBitAdder (
  input  Cin,
  input  [3:0] A,
  input  [3:0] B,
  output [3:0] Sum,
  output Cout
);

  wire twobitadder_1_cout;

  TwoBitAdder twobitadder_1 (
    .Cin(Cin), .A0(A[0]), .B0(B[0]), .A1(A[1]), .B1(B[1]), .Sum0(Sum[0]), .Cout(twobitadder_1_cout),
    .Sum1(Sum[1]));
  TwoBitAdder twobitadder_2 (
    .Cin(twobitadder_1_cout), .A0(A[2]), .B0(B[2]), .A1(A[3]), .B1(B[3]), .Sum0(Sum[2]), .Cout(Cout),
    .Sum1(Sum[3]));

  // Notes on the sheet:
  //   低位
  //   高位
endmodule

module EightBitSubtractor (
  input  [7:0] A,
  input  [7:0] B,
  output [7:0] Diff,
  output out_4
);

  wire [7:0] not_1_out;

  Adder adder_1 (.a(A), .b(not_1_out), .out(Diff), .cin(1'b1), .cout(out_4));
  assign not_1_out = ~B;  // NOT_Gate not_1, 8 bits wide
endmodule

module Multiplexer (
  input  S,
  input  D1,
  input  D0,
  output Y
);

  wire and_1_out, and_2_out, not_1_out;

  not not_1 (not_1_out, S);
  and and_1 (and_1_out, not_1_out, D0);
  and and_2 (and_2_out, S, D1);
  or or_1 (Y, and_1_out, and_2_out);
endmodule

module FourBitMultiplexer (
  input  S,
  input  [3:0] B,
  input  [3:0] A,
  output [3:0] Y
);

  Multiplexer multiplexer_1 (.S(S), .D1(B[0]), .D0(A[0]), .Y(Y[0]));
  Multiplexer multiplexer_2 (.S(S), .D1(B[1]), .D0(A[1]), .Y(Y[1]));
  Multiplexer multiplexer_3 (.S(S), .D1(B[2]), .D0(A[2]), .Y(Y[2]));
  Multiplexer multiplexer_4 (.S(S), .D1(B[3]), .D0(A[3]), .Y(Y[3]));
endmodule
