// Logisim project Lab2_Seq_Circuit_Demo_2026.circ as structural Verilog
module SR_Latch (
  input  Reset,
  input  Set,
  output Q,
  output Not_Q
);

  nor nor_1 (Q, Reset, Not_Q);
  nor nor_2 (Not_Q, Q, Set);
endmodule

module D_Latch (
  input  CLK,
  input  Data,
  output Q,
  output Not_Q
);

  wire and_1_out, and_2_out, not_1_out;

  not not_1 (not_1_out, Data);
  and and_1 (and_1_out, CLK, not_1_out);
  and and_2 (and_2_out, CLK, Data);
  SR_Latch sr_latch_1 (.Reset(and_1_out), .Set(and_2_out), .Q(Q), .Not_Q(Not_Q));
endmodule

module D_FlipFlop (
  input  CLK,
  input  Data,
  output Q,
  output Not_Q
);

  wire d_latch_1_q, not_1_out;

  not not_1 (not_1_out, CLK);
  D_Latch d_latch_1 (.CLK(not_1_out), .Data(Data), .Q(d_latch_1_q));  // open: Not_Q
  D_Latch d_latch_2 (.CLK(CLK), .Data(d_latch_1_q), .Q(Q), .Not_Q(Not_Q));

  // Notes on the sheet:
  //   主
  //   从
endmodule

module Reg_4bit (
  input  [3:0] D,
  input  CLK,
  output [3:0] out_3
);

  D_FlipFlop d_flipflop_1 (.CLK(CLK), .Data(D[0]), .Q(out_3[0]));  // open: Not_Q
  D_FlipFlop d_flipflop_2 (.CLK(CLK), .Data(D[1]), .Q(out_3[1]));  // open: Not_Q
  D_FlipFlop d_flipflop_3 (.CLK(CLK), .Data(D[2]), .Q(out_3[2]));  // open: Not_Q
  D_FlipFlop d_flipflop_4 (.CLK(CLK), .Data(D[3]), .Q(out_3[3]));  // open: Not_Q
endmodule

module play_sound_demo (
  input  \计数器复位 ,
  input  in_2,
  input  [7:0] in_3,
  input  [6:0] in_4
);

  wire clock_1_out;
  wire [7:0] counter_1_q;
  wire [13:0] rom_1_data;

  Clock clock_1 (.out(clock_1_out));
  Counter #(.max('h4)) counter_1 (
    .Q(counter_1_q), .clk(clock_1_out), .clr(\计数器复位 ));  // open: load, D, count, carry, up
  ROM #(.dataWidth(14)) rom_1 (.addr(counter_1_q), .data(rom_1_data));
  // Buzzer buzzer_1: pin names not known; wires that end beside it: rom_1_data, in_2, in_4, in_3

  // Notes on the sheet:
  //   计数器
  //   contents of rom_1 (hex, n*v repeats v):
  //   106 126 14a 15e 188
  //   Do-Re-Mi-Fa-So
  //   声音频率输入，14比特
  //   使能引脚，高电平开启
  //   调节音量大小，7比特位宽
  //   调节信号占空比，从而调节声音音色，8比特
endmodule

module D_FlipFlop_Reset (
  input  CLK,
  input  Data,
  input  Reset,
  output Q,
  output Not_Q
);

  wire and_1_out, not_1_out;

  and and_1 (and_1_out, Data, not_1_out);
  not not_1 (not_1_out, Reset);
  D_FlipFlop d_flipflop_1 (.CLK(CLK), .Data(and_1_out), .Q(Q), .Not_Q(Not_Q));

  // Notes on the sheet:
  //   带复位信号的D触发器，高电平复位
endmodule
