// Logisim project Lab3_demo (1).circ as structural Verilog: 2 circuits, main circuit main
module main (
  input  Clear,
  input  in_2,
  input  Clear_Screen,
  input  Enable,
  input  [6:0] \Y坐标 ,
  input  Reset,
  input  [7:0] B,
  input  [7:0] G,
  input  [7:0] R,
  output [3:0] \输出X坐标 ,
  output [3:0] \输出Y坐标 ,
  output [7:0] out_12
);

  wire clock_1_out, clock_2_out, clock_3_out;
  wire [6:0] adder_1_out, keyboard_1_data, register_1_q;

  Clock clock_1 (.out(clock_1_out));
  Clock clock_2 (.out(clock_2_out));
  Keyboard keyboard_1 (.clk(clock_1_out), .data(keyboard_1_data));  // open: re, clr, avail
  TTY tty_1 (.data(keyboard_1_data), .clk(clock_1_out));  // open: we, clr
  Adder #(.width(7)) adder_1 (.a(register_1_q), .b(7'b0000001), .out(adder_1_out));  // open: cin, cout
  // Probe on keyboard_1_data
  Register #(.width(7)) register_1 (.D(adder_1_out), .clk(clock_2_out), .Q(register_1_q), .clr(Reset));  // open: en
  // Probe on register_1_q
  Joystick joystick_1 (.x(\输出X坐标 ), .y(\输出Y坐标 ));
  Clock clock_3 (.out(clock_3_out));
  // RGB_Video rgb_video_1: pin names not known; wires that end beside it: Clear_Screen, clock_2_out, Enable, register_1_q, \Y坐标 , {R, G, B}
  Random random_1 (.clr(Clear), .next(in_2), .clk(clock_3_out), .out(out_12));

  // Notes on the sheet:
  //   B: initial=0xff
  //   键盘
  //   探头
  //   TTY
  //   摇杆
  //   X坐标
  //   随机数生成器
  //   RGB显示屏
endmodule

module PatternDetection_SR (
  input  Reset
);

  wire and_1_out, clock_1_out, comparator_1_eq, comparator_2_eq, comparator_3_eq;
  wire [6:0] keyboard_1_data, register_1_q, register_2_q, register_3_q;

  Clock clock_1 (.out(clock_1_out));
  Keyboard keyboard_1 (.clk(clock_1_out), .data(keyboard_1_data));  // open: re, clr, avail
  Register #(.width(7)) register_1 (.D(keyboard_1_data), .clk(clock_1_out), .Q(register_1_q), .clr(Reset));  // open: en
  Register #(.width(7)) register_2 (.D(register_1_q), .clk(clock_1_out), .Q(register_2_q), .clr(Reset));  // open: en
  Comparator #(.width(7)) comparator_1 (.a(register_1_q), .b(7'b1010101), .eq(comparator_1_eq));  // open: gt, lt
  Register #(.width(7)) register_3 (.D(register_2_q), .clk(clock_1_out), .Q(register_3_q), .clr(Reset));  // open: en
  Comparator #(.width(7)) comparator_2 (.a(register_2_q), .b(7'b1001101), .eq(comparator_2_eq));  // open: gt, lt
  Comparator #(.width(7)) comparator_3 (.a(register_3_q), .b(7'b1001010), .eq(comparator_3_eq));  // open: gt, lt
  and and_1 (and_1_out, comparator_3_eq, comparator_2_eq, comparator_1_eq);
  LED led_1 (.in(and_1_out));

  // Notes on the sheet:
  //   U?
  //   M?
  //   J?
endmodule
