// Logisim project TEST.circ as structural Verilog
module main (
);

  HalfAdder halfadder_1 ();  // open: A, B, sum, count
endmodule

module HalfAdder (
  input  A,
  input  B,
  output sum,
  output count
);

  wire and_1_out, and_2_out, not_1_out, not_2_out;

  not not_1 (not_1_out, A);
  not not_2 (not_2_out, B);
  and and_1 (and_1_out, A, not_2_out);
  and and_2 (and_2_out, not_1_out, B);
  and and_3 (count, A, B);
  or or_1 (sum, and_1_out, and_2_out);
endmodule
