// Logisim project ZUOY.circ as structural Verilog
module FULLADDER (
  input  cin,
  input  A,
  input  B,
  output cout,
  output S
);

  wire and_1_out, and_2_out, and_3_out, and_4_out, and_5_out, and_6_out, and_7_out, not_1_out, not_2_out,
       not_3_out;

  not not_1 (not_1_out, cin);
  not not_2 (not_2_out, A);
  not not_3 (not_3_out, B);
  and and_1 (and_1_out, A, B);
  and and_2 (and_2_out, cin, B);
  and and_3 (and_3_out, cin, A);
  and and_4 (and_4_out, not_1_out, not_2_out, B);
  and and_5 (and_5_out, not_1_out, A, not_3_out);
  and and_6 (and_6_out, cin, not_2_out, not_3_out);
  and and_7 (and_7_out, cin, A, B);
  or or_1 (cout, and_1_out, and_2_out, and_3_out);
  or or_2 (S, and_4_out, and_5_out, and_6_out, and_7_out);
endmodule

module TBIT (
  input  Cin0,
  input  A0,
  input  B0,
  input  A1,
  input  B1,
  output S0,
  output S1,
  output OVERFLOW
);

  wire fulladder_1_cout, fulladder_2_cout, xor_1_out;

  xor xor_1 (xor_1_out, B1, A1);
  FULLADDER fulladder_1 (.cin(Cin0), .A(A0), .B(B0), .cout(fulladder_1_cout), .S(S0));
  FULLADDER fulladder_2 (.cin(fulladder_1_cout), .A(A1), .B(B1), .cout(fulladder_2_cout), .S(S1));
  xor xor_2 (OVERFLOW, xor_1_out, fulladder_2_cout);
endmodule

module ALU (
  input  A,
  input  B,
  input  Y,
  output COUT,
  output S
);

  wire multiplexer_1_out, not_1_out;

  not not_1 (not_1_out, B);
  Multiplexer multiplexer_1 (.in0(B), .in1(not_1_out), .out(multiplexer_1_out), .sel(Y));
  FULLADDER fulladder_1 (.cin(Y), .A(A), .B(multiplexer_1_out), .cout(COUT), .S(S));
endmodule

module TALU (
  input  Y,
  input  in_2,
  input  in_3,
  input  in_4,
  input  in_5,
  output out_6,
  output out_7,
  output out_8
);

  wire multiplexer_1_out, multiplexer_2_out, not_1_out, not_2_out;

  not not_1 (not_1_out, in_3);
  Multiplexer multiplexer_1 (.in0(not_1_out), .in1(in_3), .out(multiplexer_1_out), .sel(Y));
  Multiplexer multiplexer_2 (.in0(in_5), .in1(not_2_out), .out(multiplexer_2_out), .sel(Y));
  not not_2 (not_2_out, in_5);
  TBIT tbit_1 (
    .Cin0(Y), .A0(in_2), .B0(multiplexer_1_out), .A1(in_4), .B1(multiplexer_2_out), .S0(out_6), .S1(out_7),
    .OVERFLOW(out_8));
endmodule
