// Logisim project lab2.circ as structural Verilog
module SR_Latch (
  input  Reset,
  input  Set,
  output Q,
  output Not_Q
);

  nor nor_1 (Q, Reset, Not_Q);
  nor nor_2 (Not_Q, Q, Set);
endmodule

module D_Latch (
  input  CLK,
  input  Data,
  output Q,
  output Not_Q
);

  wire and_1_out, and_2_out, not_1_out;

  not not_1 (not_1_out, Data);
  and and_1 (and_1_out, CLK, not_1_out);
  and and_2 (and_2_out, CLK, Data);
  SR_Latch sr_latch_1 (.Reset(and_1_out), .Set(and_2_out), .Q(Q), .Not_Q(Not_Q));
endmodule

module D_FlipFlop (
  input  CLK,
  input  Data,
  output Q,
  output Not_Q
);

  wire first_q, not_1_out;

  not not_1 (not_1_out, CLK);
  D_Latch first (.CLK(not_1_out), .Data(Data), .Q(first_q));  // open: Not_Q
  D_Latch d_latch_1 (.CLK(CLK), .Data(first_q), .Q(Q), .Not_Q(Not_Q));
endmodule

module D_FlipFlop_Reset (
  input  CLK,
  input  Data,
  input  Reset,
  output Q,
  output Not_Q
);

  wire and_1_out, not_1_out;

  not not_1 (not_1_out, Reset);
  and and_1 (and_1_out, Data, not_1_out);
  D_FlipFlop d_flipflop_1 (.CLK(CLK), .Data(and_1_out), .Q(Q), .Not_Q(Not_Q));
endmodule

module Reg_4bit (
  input  [3:0] in_1,
  input  CLK,
  output [3:0] out_3
);

  D_FlipFlop d_flipflop_1 (.CLK(CLK), .Data(in_1[0]), .Q(out_3[0]));  // open: Not_Q
  D_FlipFlop d_flipflop_2 (.CLK(CLK), .Data(in_1[1]), .Q(out_3[1]));  // open: Not_Q
  D_FlipFlop d_flipflop_3 (.CLK(CLK), .Data(in_1[2]), .Q(out_3[2]));  // open: Not_Q
  D_FlipFlop d_flipflop_4 (.CLK(CLK), .Data(in_1[3]), .Q(out_3[3]));  // open: Not_Q
endmodule

module CountDown_2bit (
);

  wire button_1_out, clock_1_out, comparator_1_eq, or_1_out;
  wire [3:0] multiplexer_1_out, reg_4bit_1_out_3, subtractor_1_out;

  Clock clock_1 (.out(clock_1_out));
  Reg_4bit reg_4bit_1 (.in_1(multiplexer_1_out), .CLK(clock_1_out), .out_3(reg_4bit_1_out_3));
  Subtractor #(.width(4)) subtractor_1 (.a(reg_4bit_1_out_3), .b(4'b0001), .out(subtractor_1_out));  // open: bin, bout
  Comparator #(.width(4)) comparator_1 (.a(reg_4bit_1_out_3), .b(4'b0000), .eq(comparator_1_eq));  // open: gt, lt
  Button button_1 (.out(button_1_out));
  Multiplexer #(.width(4)) multiplexer_1 (
    .in0(subtractor_1_out), .in1(4'b1001), .out(multiplexer_1_out), .sel(or_1_out));
  Hex_Digit_Display hex_digit_display_1 (.value(reg_4bit_1_out_3));  // open: dp
  or or_1 (or_1_out, comparator_1_eq, button_1_out);
endmodule

module Lantern (
  input  in_1
);

  wire clock_1_out, d_flipflop_1_q, d_flipflop_2_q, d_flipflop_3_q, d_flipflop_4_q;

  Clock clock_1 (.out(clock_1_out));
  D_FlipFlop d_flipflop_1 (.CLK(clock_1_out), .Data(in_1), .Q(d_flipflop_1_q));  // open: Not_Q
  D_FlipFlop d_flipflop_2 (.CLK(clock_1_out), .Data(d_flipflop_1_q), .Q(d_flipflop_2_q));  // open: Not_Q
  D_FlipFlop d_flipflop_3 (.CLK(clock_1_out), .Data(d_flipflop_2_q), .Q(d_flipflop_3_q));  // open: Not_Q
  D_FlipFlop d_flipflop_4 (.CLK(clock_1_out), .Data(d_flipflop_3_q), .Q(d_flipflop_4_q));  // open: Not_Q
  LED led_1 (.in(d_flipflop_1_q));
  LED led_2 (.in(d_flipflop_2_q));
  LED led_3 (.in(d_flipflop_3_q));
  LED led_4 (.in(d_flipflop_4_q));
endmodule

module Larrice (
  input  in_1,
  output [3:0] out_2
);

  wire clock_1_out;
  wire [1:0] counter_self_2bit_1_out_3;
  wire [3:0] demultiplexer_1_out0, demultiplexer_1_out1, demultiplexer_1_out2, demultiplexer_1_out3;

  Clock clock_1 (.out(clock_1_out));
  Counter_self_2bit counter_self_2bit_1 (.in_1(clock_1_out), .in_2(in_1), .out_3(counter_self_2bit_1_out_3));
  ROM #(.addrWidth(2), .dataWidth(4)) rom_1 (.addr(counter_self_2bit_1_out_3), .data(out_2));
  DotMatrix #(.matrixrows(4)) dotmatrix_1 (
    .col0(demultiplexer_1_out0), .col1(demultiplexer_1_out1), .col2(demultiplexer_1_out2),
    .col3(demultiplexer_1_out3));  // open: col4
  Demultiplexer #(.select(2), .width(4)) demultiplexer_1 (
    .out0(demultiplexer_1_out0), .out1(demultiplexer_1_out1), .out2(demultiplexer_1_out2),
    .out3(demultiplexer_1_out3), .in(out_2), .sel(counter_self_2bit_1_out_3));

  // Notes on the sheet:
  //   contents of rom_1 (hex, n*v repeats v):
  //   1 3 7 f
endmodule

module Counter_self (
  input  in_1,
  input  in_2,
  output [3:0] out_3
);

  wire [3:0] adder_1_out, multiplexer_1_out;

  Reg_4bit reg_4bit_1 (.in_1(multiplexer_1_out), .CLK(in_1), .out_3(out_3));
  Adder #(.width(4)) adder_1 (.a(out_3), .b(4'b0001), .out(adder_1_out));  // open: cin, cout
  Multiplexer #(.width(4)) multiplexer_1 (.in0(adder_1_out), .in1(4'b0000), .out(multiplexer_1_out), .sel(in_2));
endmodule

module Reg_2bit (
  input  [1:0] in_1,
  input  CLK,
  output [1:0] out_3
);

  D_FlipFlop d_flipflop_1 (.CLK(CLK), .Data(in_1[0]), .Q(out_3[0]));  // open: Not_Q
  D_FlipFlop d_flipflop_2 (.CLK(CLK), .Data(in_1[1]), .Q(out_3[1]));  // open: Not_Q
endmodule

module Counter_self_2bit (
  input  in_1,
  input  in_2,
  output [1:0] out_3
);

  wire [1:0] adder_1_out, multiplexer_1_out;

  Reg_2bit reg_2bit_1 (.in_1(multiplexer_1_out), .CLK(in_1), .out_3(out_3));
  Adder #(.width(2)) adder_1 (.a(out_3), .b(2'b01), .out(adder_1_out));  // open: cin, cout
  Multiplexer #(.width(2)) multiplexer_1 (.in0(adder_1_out), .in1(2'b00), .out(multiplexer_1_out), .sel(in_2));
endmodule
