// Logisim project test1.circ as structural Verilog
module main (
  input  in_1,
  output out_2
);

  LED led_1 (.in(out_2));
  test test_1 (.clock(in_1), .max(out_2));  // open: val, cpt

  // Notes on the sheet:
  //   说明：1）全英文路径；2）空文件夹报错（参见课堂派说明文档）
  //   3）有问题尝试，“模拟”-->“重启VHDL模拟”
endmodule

// VHDL entity test, as the project stores it:
--------------------------------------------------------------------------------
-- Project :
-- File    :
-- Autor   :
-- Date    :
--
--------------------------------------------------------------------------------
-- Description :
--
--------------------------------------------------------------------------------

LIBRARY ieee;
USE ieee.std_logic_1164.all;

ENTITY test IS
  PORT (
  ------------------------------------------------------------------------------
  --Insert input ports below
    clock      : IN  std_logic;                    -- input bit example
    val        : IN  std_logic_vector(3 DOWNTO 0); -- input vector example
  ------------------------------------------------------------------------------
  --Insert output ports below
    max        : OUT std_logic;                    -- output bit example
    cpt        : OUT std_logic_vector(3 DOWNTO 0)  -- output vector example
    );
END test;

--------------------------------------------------------------------------------
--Complete your VHDL description below
--------------------------------------------------------------------------------

ARCHITECTURE TypeArchitecture OF test IS

BEGIN

  max <= not clock;

END TypeArchitecture;
