// Logisim project vhdl_tutorial_2026Spring.circ as structural Verilog
module main (
  input  [3:0] in_1,
  input  [3:0] in_2,
  output out_3,
  output [3:0] out_4,
  output out_5,
  output [3:0] out_6,
  output out_7
);

  adder4bit adder4bit_1 (.A(in_1), .B(in_2), .carry(out_3), .sum(out_4));
  adder4bit adder4bit_2 (.A(in_1), .B(in_2), .carry(out_5), .sum(out_6));
  helloworld helloworld_1 (.clock(out_3), .max(out_7));  // open: val, cpt
  LED led_1 (.in(out_7));
endmodule

module adder4bit_testbench (
  input  [3:0] in_1,
  input  [3:0] in_2,
  output out_3,
  output [3:0] out_4
);

  adder4bit adder4bit_1 (.A(in_1), .B(in_2), .carry(out_3), .sum(out_4));
endmodule

module helloworld_testbench (
  input  in_1
);

  wire helloworld_1_max;

  helloworld helloworld_1 (.clock(in_1), .max(helloworld_1_max));  // open: val, cpt
  LED led_1 (.in(helloworld_1_max));
endmodule

module you_xian_ji_testbench (
  input  in_1,
  input  in_2,
  input  in_3,
  output out_4
);

  you_xian_ji you_xian_ji_1 (.a(in_1), .b(in_2), .c(in_3), .y(out_4));
endmodule

module quan_jia_qi_testbench (
  input  in_1,
  input  in_2,
  input  in_3,
  output out_4,
  output out_5
);

  quan_jia_qi quan_jia_qi_1 (.a(in_1), .b(in_2), .cin(in_3), .sum(out_4), .cout(out_5));
endmodule

module quan_jia_qi_2_testbench (
  input  in_1,
  input  in_2,
  input  in_3,
  output out_4,
  output out_5
);

  quan_jia_qi_2 quan_jia_qi_2_1 (.a(in_1), .b(in_2), .cin(in_3), .sum(out_4), .cout(out_5));
endmodule

module adder4bit_jiegou_testbench (
  input  [3:0] in_1,
  input  [3:0] in_2,
  output out_3,
  output [3:0] out_4
);

  adder4bit_jiegou adder4bit_jiegou_1 (.A(in_1), .B(in_2), .carry(out_3), .sum(out_4));
endmodule

module qi_duan_shu_ma_guan_testbench (
  input  [3:0] in_1
);

  wire qi_duan_shu_ma_guan_1_o_segment_a, qi_duan_shu_ma_guan_1_o_segment_b,
       qi_duan_shu_ma_guan_1_o_segment_c, qi_duan_shu_ma_guan_1_o_segment_d,
       qi_duan_shu_ma_guan_1_o_segment_e, qi_duan_shu_ma_guan_1_o_segment_f,
       qi_duan_shu_ma_guan_1_o_segment_g;

  qi_duan_shu_ma_guan qi_duan_shu_ma_guan_1 (
    .i_Binary_Num(in_1), .o_Segment_A(qi_duan_shu_ma_guan_1_o_segment_a),
    .o_Segment_B(qi_duan_shu_ma_guan_1_o_segment_b), .o_Segment_C(qi_duan_shu_ma_guan_1_o_segment_c),
    .o_Segment_D(qi_duan_shu_ma_guan_1_o_segment_d), .o_Segment_E(qi_duan_shu_ma_guan_1_o_segment_e),
    .o_Segment_F(qi_duan_shu_ma_guan_1_o_segment_f), .o_Segment_G(qi_duan_shu_ma_guan_1_o_segment_g));
  _7_Segment_Display u_7_segment_display_1 (
    .g(qi_duan_shu_ma_guan_1_o_segment_g), .f(qi_duan_shu_ma_guan_1_o_segment_f),
    .a(qi_duan_shu_ma_guan_1_o_segment_a), .b(qi_duan_shu_ma_guan_1_o_segment_b),
    .e(qi_duan_shu_ma_guan_1_o_segment_e), .d(qi_duan_shu_ma_guan_1_o_segment_d),
    .c(qi_duan_shu_ma_guan_1_o_segment_c));  // open: dp
endmodule

module ji_cun_qi_testbench (
  input  [3:0] in_1,
  output [3:0] out_2
);

  wire clock_1_out;

  Clock clock_1 (.out(clock_1_out));
  ji_cun_qi ji_cun_qi_1 (.clock(clock_1_out), .d(in_1), .q(out_2));
endmodule

module ji_shu_qi_testbench (
  input  in_1,
  output [3:0] out_2
);

  wire clock_1_out;

  Clock clock_1 (.out(clock_1_out));
  Hex_Digit_Display hex_digit_display_1 (.value(out_2));  // open: dp
  ji_shu_qi ji_shu_qi_1 (.clk(clock_1_out), .reset(in_1), .q(out_2));
endmodule

module you_xian_zhuang_tai_ji_testbench (
  input  in_1,
  input  in_2,
  output out_3
);

  wire clock_1_out;

  Clock clock_1 (.out(clock_1_out));
  you_xian_zhuang_tai_ji you_xian_zhuang_tai_ji_1 (.clk(clock_1_out), .reset(in_1), .in0(in_2), .y(out_3));
endmodule

// VHDL entity adder4bit, as the project stores it:
--------------------------------------------------------------------------------
-- Project :
-- File    :
-- Autor   :
-- Date    :
--
--------------------------------------------------------------------------------
-- Description :
-- 利用std_logic_vector实现4位加法器
--------------------------------------------------------------------------------

LIBRARY ieee;
USE ieee.std_logic_1164.all;

use ieee.numeric_std_unsigned.all;  -- 提供+运算符并按无符号处理

ENTITY adder4bit IS
  PORT (
  ------------------------------------------------------------------------------
  --Insert input ports below
	A	     : IN  std_logic_vector(3 DOWNTO 0); 
	B		: IN  std_logic_vector(3 DOWNTO 0); 
  ------------------------------------------------------------------------------
  --Insert output ports below
	carry	: OUT std_logic;                    
	sum		: OUT std_logic_vector(3 DOWNTO 0)
    );
END adder4bit;

--------------------------------------------------------------------------------
--Complete your VHDL description below
--------------------------------------------------------------------------------

ARCHITECTURE behv OF adder4bit IS

-- define a temparary signal to store the result
signal result: std_logic_vector(4 downto 0);

BEGIN

    -- the highest bit should be carry
    result <= ('0' & A)+('0' & B);
    sum <= result(3 downto 0);
    carry <= result(4);

END behv;

// VHDL entity helloworld, as the project stores it:
--------------------------------------------------------------------------------
-- Project :
-- File    :
-- Autor   :
-- Date    :
--
--------------------------------------------------------------------------------
-- Description :
-- Logisim默认生成的VHDL代码模板稍作修改
--------------------------------------------------------------------------------

LIBRARY ieee;
USE ieee.std_logic_1164.all;

ENTITY helloworld IS
  PORT (
  ------------------------------------------------------------------------------
  --Insert input ports below
    clock      : IN  std_logic;                    -- input bit example
    val        : IN  std_logic_vector(3 DOWNTO 0); -- input vector example
  ------------------------------------------------------------------------------
  --Insert output ports below
    max        : OUT std_logic;                    -- output bit example
    cpt        : OUT std_logic_vector(3 DOWNTO 0)  -- output vector example
    );
END helloworld;

--------------------------------------------------------------------------------
--Complete your VHDL description below
--------------------------------------------------------------------------------

ARCHITECTURE TypeArchitecture OF helloworld IS

BEGIN
  max <= not clock;

END TypeArchitecture;

// VHDL entity you_xian_ji, as the project stores it:
--------------------------------------------------------------------------------
-- Project :
-- File    :
-- Autor   :
-- Date    :
--
--------------------------------------------------------------------------------
-- Description :
-- 运算符优先级示例
--------------------------------------------------------------------------------

LIBRARY ieee;
USE ieee.std_logic_1164.all;

ENTITY you_xian_ji IS
  PORT (
  ------------------------------------------------------------------------------
  --Insert input ports below
    a      : IN  std_logic;                    -- input bit example
    b      : IN  std_logic;                    -- input bit example
    c      : IN  std_logic;                    -- input bit example
  ------------------------------------------------------------------------------
  --Insert output ports below
    y        : OUT std_logic                    -- output bit example
    );
END you_xian_ji;

--------------------------------------------------------------------------------
--Complete your VHDL description below
--------------------------------------------------------------------------------

ARCHITECTURE TypeArchitecture OF you_xian_ji IS

BEGIN
   y <= a or (b and c);

END TypeArchitecture;

// VHDL entity quan_jia_qi, as the project stores it:
--------------------------------------------------------------------------------
-- Project :
-- File    :
-- Autor   :
-- Date    :
--
--------------------------------------------------------------------------------
-- Description :
-- 利用逻辑运算构建的全加器
--------------------------------------------------------------------------------

LIBRARY ieee;
USE ieee.std_logic_1164.all;

ENTITY quan_jia_qi IS
  PORT (
  ------------------------------------------------------------------------------
  --Insert input ports below
    a     : IN  std_logic;                  -- input bit example
    b     : IN  std_logic;                  -- input bit example
    cin   : IN  std_logic;                  -- input bit example
  ------------------------------------------------------------------------------
  --Insert output ports below
    sum   : OUT std_logic;                  -- output bit example
    cout  : OUT std_logic                   -- output bit example
    );
END quan_jia_qi;

--------------------------------------------------------------------------------
--Complete your VHDL description below
--------------------------------------------------------------------------------

ARCHITECTURE TypeArchitecture OF quan_jia_qi IS

BEGIN
    
    sum  <= a xor b xor cin;
    cout <= (a and b) or (a and cin) or (b and cin);    
    
END TypeArchitecture;

// VHDL entity quan_jia_qi_2, as the project stores it:
--------------------------------------------------------------------------------
-- Project :
-- File    :
-- Autor   :
-- Date    :
--
--------------------------------------------------------------------------------
-- Description :
-- 利用算术运算符构建的全加器
--------------------------------------------------------------------------------

LIBRARY ieee;
USE ieee.std_logic_1164.all;

use ieee.numeric_std_unsigned.all;  -- 提供+运算符并按无符号处理

ENTITY quan_jia_qi_2 IS
  PORT (
  ------------------------------------------------------------------------------
  --Insert input ports below
    a     : IN  std_logic;                    -- input bit example
    b     : IN  std_logic;                    -- input bit example
    cin     : IN  std_logic;                    -- input bit example
  ------------------------------------------------------------------------------
  --Insert output ports below
    sum        : OUT std_logic;                    -- output bit example
    cout        : OUT std_logic                    -- output bit example
    );
END quan_jia_qi_2;

--------------------------------------------------------------------------------
--Complete your VHDL description below
--------------------------------------------------------------------------------

ARCHITECTURE TypeArchitecture OF quan_jia_qi_2 IS

    -- define a temparary signal to store the result
    signal result: std_logic_vector(1 downto 0);

BEGIN

    result <= ("0" & a) + ("0" & b) + ("0" & cin); -- + 是算术运算，&用于补齐位宽
    sum <= result(0);  -- result的低位是sum
    cout <= result(1); -- result的高位是cout

END TypeArchitecture;

// VHDL entity adder4bit_jiegou, as the project stores it:
--------------------------------------------------------------------------------
-- Project :
-- File    :
-- Autor   :
-- Date    :
--
--------------------------------------------------------------------------------
-- Description :
-- 4比特加法器的结构建模示例
--------------------------------------------------------------------------------

LIBRARY ieee;
USE ieee.std_logic_1164.all;

ENTITY adder4bit_jiegou IS
  PORT (
  ------------------------------------------------------------------------------
  --Insert input ports below
	A	     : IN  std_logic_vector(3 DOWNTO 0); 
	B		: IN  std_logic_vector(3 DOWNTO 0); 
  ------------------------------------------------------------------------------
  --Insert output ports below
	carry	: OUT std_logic;                    
	sum		: OUT std_logic_vector(3 DOWNTO 0)
    );
END adder4bit_jiegou;

--------------------------------------------------------------------------------
--Complete your VHDL description below
--------------------------------------------------------------------------------

ARCHITECTURE behv OF adder4bit_jiegou IS

COMPONENT quan_jia_qi
  PORT (
  ------------------------------------------------------------------------------
  --Insert input ports below
    a     : IN  std_logic;                   
    b     : IN  std_logic;                    
    cin   : IN  std_logic;                    
  ------------------------------------------------------------------------------
  --Insert output ports below
    sum        : OUT std_logic;                    
    cout       : OUT std_logic                    
    );
END COMPONENT quan_jia_qi;

-- define a temparary signal to store the result
signal result: std_logic_vector(4 downto 0);
signal n0, n1, n2: std_logic;

BEGIN
 
    adder0: quan_jia_qi port map(A(0), B(0), '0', result(0), n0);
    adder1: quan_jia_qi port map(A(1), B(1),  n0, result(1), n1);
    adder2: quan_jia_qi port map(A(2), B(2),  n1, result(2), n2);
    adder3: quan_jia_qi port map(A(3), B(3),  n2, result(3), result(4));
    
    -- the highest bit should be carry
    sum   <= result(3 downto 0);
    carry <= result(4);

END behv;

// VHDL entity qi_duan_shu_ma_guan, as the project stores it:
--------------------------------------------------------------------------------
-- Project :
-- File    :
-- Autor   :
-- Date    :
--
--------------------------------------------------------------------------------
-- Description :
--
--------------------------------------------------------------------------------

LIBRARY ieee;
USE ieee.std_logic_1164.all;

ENTITY qi_duan_shu_ma_guan IS
  PORT (
    i_Binary_Num : in  std_logic_vector(3 downto 0);
    o_Segment_A  : out std_logic;
    o_Segment_B  : out std_logic;
    o_Segment_C  : out std_logic;
    o_Segment_D  : out std_logic;
    o_Segment_E  : out std_logic;
    o_Segment_F  : out std_logic;
    o_Segment_G  : out std_logic
    );
END qi_duan_shu_ma_guan;

--------------------------------------------------------------------------------
--Complete your VHDL description below
--------------------------------------------------------------------------------

ARCHITECTURE TypeArchitecture OF qi_duan_shu_ma_guan IS

    signal LED_out : std_logic_vector(6 downto 0) := (others => '0');

BEGIN

process(i_Binary_Num)						--decoder bcd-7segment
  begin
    case i_Binary_Num is -- from a to g
      when "0000" => LED_out <= "1111110"; -- 0     
      when "0001" => LED_out <= "0110000"; -- 1 
      when "0010" => LED_out <= "1101101"; -- 2 
      when "0011" => LED_out <= "1111001"; -- 3 
      when "0100" => LED_out <= "0110011"; -- 4 
      when "0101" => LED_out <= "1011011"; -- 5 
      when "0110" => LED_out <= "1011111"; -- 6 
      when "0111" => LED_out <= "1110000"; -- 7 
      when "1000" => LED_out <= "1111111"; -- 8     
      when "1001" => LED_out <= "1110011"; -- 9
      when others => LED_out <= "0000000"; -- A~F
    end case;
end process;

  o_Segment_A <= LED_out(6);
  o_Segment_B <= LED_out(5);
  o_Segment_C <= LED_out(4);
  o_Segment_D <= LED_out(3);
  o_Segment_E <= LED_out(2);
  o_Segment_F <= LED_out(1);
  o_Segment_G <= LED_out(0);

END TypeArchitecture;

// VHDL entity ji_cun_qi, as the project stores it:
--------------------------------------------------------------------------------
-- Project :
-- File    :
-- Autor   :
-- Date    :
--
--------------------------------------------------------------------------------
-- Description :
-- 寄存器
--------------------------------------------------------------------------------

LIBRARY ieee;
USE ieee.std_logic_1164.all;

ENTITY ji_cun_qi IS
  PORT (
  ------------------------------------------------------------------------------
  --Insert input ports below
    clock      : IN  std_logic;                    -- input bit example
    d          : IN  std_logic_vector(3 DOWNTO 0); -- input vector example
  ------------------------------------------------------------------------------
  --Insert output ports below
    q          : OUT std_logic_vector(3 DOWNTO 0)  -- output vector example
    );
END ji_cun_qi;

--------------------------------------------------------------------------------
--Complete your VHDL description below
--------------------------------------------------------------------------------

ARCHITECTURE TypeArchitecture OF ji_cun_qi IS

BEGIN
  
  process(clock) begin
    if rising_edge(clock) then --rising_edge()用于获取clock的上升沿
      q <= d;
    end if;
  end process;

END TypeArchitecture;

// VHDL entity ji_shu_qi, as the project stores it:
--------------------------------------------------------------------------------
-- Project :
-- File    :
-- Autor   :
-- Date    :
--
--------------------------------------------------------------------------------
-- Description :
-- 同步复位计数器
--------------------------------------------------------------------------------

LIBRARY ieee;
USE ieee.std_logic_1164.all;

USE ieee.numeric_std_unsigned.all;  -- 提供+运算符并按无符号处理

ENTITY ji_shu_qi IS
  PORT (
  ------------------------------------------------------------------------------
  --Insert input ports below
    clk, reset      : IN  std_logic;                    -- input bit example
  ------------------------------------------------------------------------------
  --Insert output ports below
    q               : OUT std_logic_vector(3 DOWNTO 0)  -- output vector example
    );
END ji_shu_qi;

--------------------------------------------------------------------------------
--Complete your VHDL description below
--------------------------------------------------------------------------------

ARCHITECTURE TypeArchitecture OF ji_shu_qi IS

  signal counter              : std_logic_vector(3 DOWNTO 0);

BEGIN

  process(clk) begin
    if reset = '1' then
      counter <= (OTHERS => '0');
    elsif rising_edge(clk) then
      counter <= counter +'1';
    end if;
  end process;

  q <= counter;

END TypeArchitecture;

// VHDL entity you_xian_zhuang_tai_ji, as the project stores it:
--------------------------------------------------------------------------------
-- Project :
-- File    :
-- Autor   :
-- Date    :
--
--------------------------------------------------------------------------------
-- Description :
-- 一个简单的有限状态机的示例 (异步复位)
--------------------------------------------------------------------------------

LIBRARY ieee;
USE ieee.std_logic_1164.all;

ENTITY you_xian_zhuang_tai_ji IS
  PORT (
  ------------------------------------------------------------------------------
  --Insert input ports below
    clk, reset      : IN  std_logic;                    
    in0             : IN  std_logic; 
  ------------------------------------------------------------------------------
  --Insert output ports below
    y        : OUT std_logic                    -- output bit example
    );
END you_xian_zhuang_tai_ji;

--------------------------------------------------------------------------------
--Complete your VHDL description below
--------------------------------------------------------------------------------

ARCHITECTURE TypeArchitecture OF you_xian_zhuang_tai_ji IS

  type statetype is (IDLE, S0, S1);
  signal state, nextstate: statetype;

BEGIN

  -- 状态寄存器的更新
  process(clk, reset) begin
    if reset = '1' then
      state <= IDLE;
    elsif rising_edge(clk) then
      state <= nextstate;
    end if;
  end process;

  -- 组合逻辑：计算下一个状态
  process(state) begin
    case state is
      when IDLE =>
        if in0 = '0' then 	nextstate <= IDLE;
        else			     nextstate <= S0;
        end if;
      when S0 =>
        if in0 = '0' then 	nextstate <= IDLE;
        else				nextstate <= S1;
        end if;
      when S1 =>
        if in0 = '0' then 	nextstate <= IDLE;
        else				nextstate <= S1;
        end if;
      when others =>		nextstate <= IDLE;  
    end case;  
  end process;

  -- 组合逻辑：计算输出
  y <= '1' when state = S1 else '0';

END TypeArchitecture;

// VHDL entity vhdl_testbench_example, as the project stores it:
--------------------------------------------------------------------------------
-- Project :
-- File    :
-- Autor   :
-- Date    :
--
--------------------------------------------------------------------------------
-- Description :
-- 使用代码编写测试程序
--------------------------------------------------------------------------------

library ieee;
use ieee.std_logic_1164.all;

entity vhdl_testbench_example is				-- entity declaration
end vhdl_testbench_example;

architecture TB of vhdl_testbench_example is

  component adder4bit
    PORT (
    ------------------------------------------------------------------------------
    --Insert input ports below
     	A	     : IN  std_logic_vector(3 DOWNTO 0); 
	     B		: IN  std_logic_vector(3 DOWNTO 0); 
    ------------------------------------------------------------------------------
    --Insert output ports below
	     carry	: OUT std_logic;                    
	     sum		: OUT std_logic_vector(3 DOWNTO 0)
        );
  END component adder4bit;

    signal A, B:	std_logic_vector(3 downto 0);
    signal carry:	std_logic;
    signal sum:	std_logic_vector(3 downto 0);

begin

    dut: adder4bit port map (A, B, carry, sum);

    process			
	
	  variable err_cnt: integer :=0;
    
    begin												  
		
	  -- case 1
	  A <= "0000";							
	  B <= "0000";
	  wait for 10 ns;
	  assert (sum="0000") report "Sum Error!" severity error;
	  assert (carry='0') report "Carry Error!" severity error;
	  if (sum/="0000" or carry/='0') then
	    err_cnt:=err_cnt+1;
	  end if;
	  	
 	  -- case 2 		
	  A <= "0011";
	  B <= "0011";
	  wait for 10 ns;												  
	  assert (sum="0110") report "Sum Error!" severity error;	 
	  assert (carry='0') report "Carry Error!" severity error;
	  if (sum/="0110" or carry/='0') then
	    err_cnt:=err_cnt+1;
	  end if;
		
	  -- case 3
	  A <= "0001";
	  B <= "0010";
	  wait for 10 ns;												  
	  assert (sum="0011") report "Sum Error!" severity error;	 
	  assert (carry='0') report "Carry Error!" severity error;
	  if (sum/="0011" or carry/='0') then
	    err_cnt:=err_cnt+1;
	  end if;
		
	  -- case 4
	  A <= "0010";
	  B <= "0001";
	  wait for 10 ns;												  
	  assert (sum="0011") report "Sum Error!" severity error;	 
	  assert (carry='0') report "Carry Error!" severity error;
	  if (sum/="0011" or carry/='0') then
	    err_cnt:=err_cnt+1;
	  end if;
		
	  -- case 5
	  A <= "0001";
	  B <= "0001";
	  wait for 10 ns;
	  assert (sum="0010") report "Sum Error!" severity error;
	  assert (carry='0') report "Carry Error!" severity error;
	  if (sum/="0010" or carry/='0') then
	    err_cnt:=err_cnt+1;
	  end if;
		
	  -- summary of testbench
	  if (err_cnt=0) then
	    assert false
	    report "Testbench of Adder completed successfully!"
	    severity note;
	  else
	    assert true
	    report "Something wrong, try again"
	    severity error;
	  end if;			
	wait; 
		
    end process;
	
end TB;

// VHDL entity test2, as the project stores it:
--------------------------------------------------------------------------------
-- Project :
-- File    :
-- Autor   :
-- Date    :
--
--------------------------------------------------------------------------------
-- Description :
--
--------------------------------------------------------------------------------

LIBRARY ieee;
USE ieee.std_logic_1164.all;

ENTITY test2 IS
  PORT (
  ------------------------------------------------------------------------------
  --Insert input ports below
    clock      : IN  std_logic;                    -- input bit example
    val        : IN  std_logic_vector(3 DOWNTO 0); -- input vector example
  ------------------------------------------------------------------------------
  --Insert output ports below
    max        : OUT std_logic;                    -- output bit example
    cpt        : OUT std_logic_vector(3 DOWNTO 0)  -- output vector example
    );
END test2;

--------------------------------------------------------------------------------
--Complete your VHDL description below
--------------------------------------------------------------------------------

ARCHITECTURE TypeArchitecture OF test2 IS

BEGIN
    max <= not clock;

END TypeArchitecture;
