// Logisim project zuoye_fixed.circ as structural Verilog: 2 circuits, main circuit TBIT
module FULLADDER (
  input  Cin,
  input  B,
  input  A,
  output Cout,
  output S
);

  wire or_1_out;

  // XOR_Gate xor_1 is placed but not wired
  and and_1 (A, A, A);
  buf and_2 (Cin, Cin);  // AND_Gate
  // XOR_Gate xor_2 is placed but not wired
  // OR_Gate or_1 has open pins: out=or_1_out

  assign B = A;
endmodule

module TBIT (
  input  CIN0,
  input  B0,
  input  A0,
  input  B1,
  input  A1,
  output S0,
  output S1,
  output overflow
);

  wire fulladder_2_p2, xor_1_p2;

  // FULLADDER fulladder_1: pin names not known; wires that end beside it: B0, CIN0, A0
  // FULLADDER fulladder_2: pin names not known; wires that end beside it: B1, fulladder_2_p2, A1
  // XOR_Gate xor_1: pin names not known; wires that end beside it: fulladder_2_p2, xor_1_p2, overflow
endmodule
