// Logisim project workdesign_fixed.circ as structural Verilog
module main (
  input  in_1
);

  wire button_1_out, button_2_out, clock_1_out, dotmatrix_1_p12, model4_1_at_bottom, model5_1_hit,
       model6_1_grn, model6_1_red, model6_1_run;
  wire [3:0] model2_1_src_pin, model3_1_car_pos, model7_1_score1_q, model7_1_score10_q, random_1_out;
  wire [15:0] decoder_1_out0, decoder_2_out0, decoder_3_out0, dotmatrix_1_p13;

  Clock clock_1 (.out(clock_1_out));
  Button button_1 (.out(button_1_out));
  Button button_2 (.out(button_2_out));
  Random #(.width(4)) random_1 (.clk(clock_1_out), .out(random_1_out));  // open: clr, next
  model8 model8_1 ();  // open: CAR_COL, OBS_COL, OBS_ROW, RST, ROW_ADDR, COL_DATA
  model2 model2_1 (.SRC_PIN(model2_1_src_pin));
  Decoder #(.select(4)) decoder_1 (
    .out0(decoder_1_out0[0]), .out1(decoder_1_out0[1]), .out2(decoder_1_out0[2]), .out3(decoder_1_out0[3]),
    .out4(decoder_1_out0[4]), .out5(decoder_1_out0[5]), .out6(decoder_1_out0[6]), .out7(decoder_1_out0[7]),
    .out8(decoder_1_out0[8]), .out9(decoder_1_out0[9]), .out10(decoder_1_out0[10]),
    .out11(decoder_1_out0[11]), .out12(decoder_1_out0[12]), .out13(decoder_1_out0[13]),
    .out14(decoder_1_out0[14]), .out15(decoder_1_out0[15]), .sel(random_1_out));  // open: en
  model3 model3_1 (.LEFT(button_1_out), .RIGHT(button_2_out), .Reset(in_1), .car_pos(model3_1_car_pos));
  Decoder #(.select(4)) decoder_2 (
    .out0(decoder_2_out0[0]), .out1(decoder_2_out0[1]), .out2(decoder_2_out0[2]), .out3(decoder_2_out0[3]),
    .out4(decoder_2_out0[4]), .out5(decoder_2_out0[5]), .out6(decoder_2_out0[6]), .out7(decoder_2_out0[7]),
    .out8(decoder_2_out0[8]), .out9(decoder_2_out0[9]), .out10(decoder_2_out0[10]),
    .out11(decoder_2_out0[11]), .out12(decoder_2_out0[12]), .out13(decoder_2_out0[13]),
    .out14(decoder_2_out0[14]), .out15(decoder_2_out0[15]));  // open: sel, en
  model4 model4_1 (.OBS_SRC(model2_1_src_pin), .Reset(in_1), .AT_BOTTOM(model4_1_at_bottom));  // open: out_3
  // DotMatrix #(.inputtype("select"), .matrixcols(16), .matrixrows(16)) dotmatrix_1: pin names not known; wires that end beside it: decoder_1_out0[5], decoder_1_out0[6], decoder_1_out0[7], decoder_1_out0[8], decoder_1_out0[10], decoder_1_out0[11], decoder_1_out0[12], decoder_1_out0[13], decoder_1_out0[14], decoder_1_out0[15], decoder_1_out0[4], dotmatrix_1_p12, dotmatrix_1_p13, dotmatrix_1_p12, model3_1_car_pos, decoder_1_out0, decoder_2_out0
  model5 model5_1 (.X(model3_1_car_pos), .Y(model3_1_car_pos), .At_Botton(model4_1_at_bottom), .hit(model5_1_hit));
  Decoder #(.select(4)) decoder_3 (
    .out0(decoder_3_out0[0]), .out1(decoder_3_out0[1]), .out2(decoder_3_out0[2]), .out3(decoder_3_out0[3]),
    .out4(decoder_3_out0[4]), .out5(decoder_3_out0[5]), .out6(decoder_3_out0[6]), .out7(decoder_3_out0[7]),
    .out8(decoder_3_out0[8]), .out9(decoder_3_out0[9]), .out10(decoder_3_out0[10]),
    .out11(decoder_3_out0[11]), .out12(decoder_3_out0[12]), .out13(decoder_3_out0[13]),
    .out14(decoder_3_out0[14]), .out15(decoder_3_out0[15]), .sel(4'b0000));  // open: en
  model6 model6_1 (.HIT(model5_1_hit), .RUN(model6_1_run), .GRN(model6_1_grn), .RED(model6_1_red));
  Hex_Digit_Display hex_digit_display_1 (.value(model7_1_score10_q));  // open: dp
  model7 model7_1 (
    .AT_BOTTOM(model4_1_at_bottom), .HIT(model5_1_hit), .RUNNING(model6_1_run), .SCORE1_Q(model7_1_score1_q),
    .SCORE10_Q(model7_1_score10_q));
  LED led_1 (.in(model6_1_grn));
  LED led_2 (.in(model6_1_red));
  Hex_Digit_Display hex_digit_display_2 (.value(model7_1_score1_q));  // open: dp
endmodule

module Input_system (
  input  SPEED0,
  input  SPEED1
);

  Clock CLK ();  // open: out
  Button LEFT ();  // open: out
  Button RIGHT ();  // open: out
  Button START ();  // open: out
  Button RST ();  // open: out
endmodule

module module1 (
  input  [1:0] in_1,
  output [3:0] out_2
);

  wire clock_1_out;
  wire [3:0] adder_1_out, adder_2_out, adder_3_out, CNT1_q, CNT2_q, CNT3_q;

  Clock clock_1 (.out(clock_1_out));
  Adder #(.width(4)) adder_1 (.a(CNT1_q), .b(4'b0001), .out(adder_1_out));  // open: cin, cout
  Adder #(.width(4)) adder_2 (.a(CNT1_q), .b(CNT1_q), .out(adder_2_out));  // open: cin, cout
  Adder #(.width(4)) adder_3 (.a(CNT2_q), .b(CNT1_q), .out(adder_3_out));  // open: cin, cout
  Register #(.width(4)) CNT1 (.D(adder_1_out), .clk(clock_1_out), .Q(CNT1_q));  // open: en, clr
  Register #(.width(4)) CNT2 (.D(adder_2_out), .clk(clock_1_out), .Q(CNT2_q));  // open: en, clr
  Register #(.width(4)) CNT3 (.D(adder_3_out), .clk(clock_1_out), .Q(CNT3_q));  // open: en, clr
  Multiplexer #(.select(2), .width(4)) multiplexer_1 (
    .in1(CNT1_q), .in2(CNT2_q), .in3(CNT3_q), .out(out_2), .sel(in_1));  // open: in0
endmodule

module model2 (
  output [3:0] SRC_PIN
);

  wire clock_1_out;
  wire [3:0] adder_1_out;

  Clock clock_1 (.out(clock_1_out));
  Register #(.width(4)) OBS_SRC (.D(adder_1_out), .clk(clock_1_out), .Q(SRC_PIN));  // open: en, clr
  Adder #(.width(4)) adder_1 (.a(SRC_PIN), .b(4'b0011), .out(adder_1_out));  // open: cin, cout
endmodule

module model3 (
  input  LEFT,
  input  RIGHT,
  input  Reset,
  output [3:0] car_pos
);

  wire clock_1_out, comparator_1_gt, comparator_1_lt, comparator_2_gt, comparator_2_lt, or_1_out, or_2_out;
  wire [1:0] and_2_out;
  wire [3:0] adder_1_out, multiplexer_1_out, multiplexer_2_out;

  Multiplexer #(.select(2), .width(4)) multiplexer_1 (
    .in0(4'b0000), .in1(4'b1111), .in2(4'b0001), .in3(4'b0000), .out(multiplexer_1_out), .sel(and_2_out));
  Clock clock_1 (.out(clock_1_out));
  Adder #(.width(4)) adder_1 (.a(multiplexer_1_out), .b(car_pos), .out(adder_1_out));  // open: cin, cout
  Multiplexer #(.width(4)) multiplexer_2 (.in0(adder_1_out), .in1(4'b1000), .out(multiplexer_2_out), .sel(Reset));
  Register #(.width(4)) register_1 (.D(multiplexer_2_out), .clk(clock_1_out), .Q(car_pos));  // open: en, clr
  Comparator #(.width(4)) comparator_1 (
    .a(car_pos), .b(4'b0000), .gt(comparator_1_gt), .lt(comparator_1_lt));  // open: eq
  Comparator #(.width(4)) comparator_2 (
    .a(car_pos), .b(4'b1111), .gt(comparator_2_gt), .lt(comparator_2_lt));  // open: eq
  or or_1 (or_1_out, comparator_1_gt, comparator_1_lt);
  or or_2 (or_2_out, comparator_2_gt, comparator_2_lt);
  and and_1 (and_2_out[1], or_2_out, RIGHT);
  and and_2 (and_2_out[0], LEFT, or_1_out);
endmodule

module model4 (
  input  [3:0] OBS_SRC,
  input  Reset,
  output [3:0] out_3,
  output AT_BOTTOM
);

  wire clock_1_out;
  wire [3:0] adder_1_out, OBS_COL_q;

  Clock clock_1 (.out(clock_1_out));
  Register #(.width(4)) OBS_COL (.D(OBS_SRC), .en(clock_1_out), .clk(clock_1_out), .Q(OBS_COL_q), .clr(Reset));
  Register #(.width(4)) OBS_ROW (.D(adder_1_out), .en(clock_1_out), .clk(clock_1_out), .Q(out_3), .clr(Reset));
  Adder #(.width(4)) adder_1 (.a(OBS_COL_q), .b(4'b0001), .out(adder_1_out));  // open: cin, cout
  Comparator #(.width(4)) comparator_1 (.a(out_3), .b(4'b1111), .eq(AT_BOTTOM));  // open: gt, lt
endmodule

module model5 (
  input  [3:0] X,
  input  [3:0] Y,
  input  At_Botton,
  output hit
);

  wire comparator_1_eq;

  Comparator #(.width(4)) comparator_1 (.a(X), .b(Y), .eq(comparator_1_eq));  // open: gt, lt
  and and_1 (hit, comparator_1_eq, At_Botton);
endmodule

module model6 (
  input  HIT,
  output RUN,
  output GRN,
  output RED
);

  wire and_1_out, clock_1_out, KEEP_out, not_1_out, not_2_out, not_3_out, S0_out, START_out;

  Clock clock_1 (.out(clock_1_out));
  not not_1 (not_1_out, HIT);
  and and_1 (and_1_out, RED, not_1_out);
  and KEEP (KEEP_out, HIT, RED);
  or S0 (S0_out, START_out, and_1_out);
  D_Flip_Flop FF_S1 (.D(KEEP_out), .clk(clock_1_out), .Q(GRN));  // open: Qn, preset, reset
  D_Flip_Flop FF_S0 (.D(S0_out), .clk(clock_1_out), .Q(RED));  // open: Qn, preset, reset
  not not_2 (not_2_out, GRN);
  not not_3 (not_3_out, RED);
  and START (START_out, not_2_out, not_3_out);

  assign RUN = HIT;
endmodule

module model7 (
  input  AT_BOTTOM,
  input  HIT,
  input  RUNNING,
  output [3:0] SCORE1_Q,
  output [3:0] SCORE10_Q
);

  wire and_1_out, clock_1_out, comparator_1_eq, comparator_2_eq;
  wire [3:0] adder_1_out, adder_2_out, multiplexer_1_out, multiplexer_2_out, multiplexer_3_out,
       multiplexer_4_out, subtractor_1_out;

  Clock clock_1 (.out(clock_1_out));
  Multiplexer #(.width(4)) multiplexer_1 (
    .in0(subtractor_1_out), .in1(adder_1_out), .out(multiplexer_1_out), .sel(and_1_out));
  Multiplexer #(.width(4)) multiplexer_2 (
    .in0(adder_2_out), .in1(4'b0000), .out(multiplexer_2_out), .sel(comparator_1_eq));
  Subtractor #(.width(4)) subtractor_1 (.a(adder_1_out), .b(4'b0001), .out(subtractor_1_out));  // open: bin, bout
  Register #(.width(4)) SCORE1 (.D(multiplexer_3_out), .clk(clock_1_out), .Q(SCORE1_Q));  // open: en, clr
  Multiplexer #(.width(4)) multiplexer_3 (
    .in0(multiplexer_1_out), .in1(4'b0000), .out(multiplexer_3_out), .sel(comparator_2_eq));
  Register #(.width(4)) SCORE10 (.D(multiplexer_2_out), .clk(clock_1_out), .Q(SCORE10_Q));  // open: en, clr
  Adder #(.width(4)) adder_1 (.a(4'b0001), .b(SCORE1_Q), .out(adder_1_out));  // open: cin, cout
  and and_1 (and_1_out, AT_BOTTOM, HIT, RUNNING);
  Multiplexer #(.width(4)) multiplexer_4 (.in0(4'b0000), .in1(4'b0001), .out(multiplexer_4_out), .sel(comparator_2_eq));
  Comparator #(.width(4)) comparator_1 (.a(SCORE10_Q), .b(4'b1001), .eq(comparator_1_eq));  // open: gt, lt
  Adder #(.width(4)) adder_2 (.a(SCORE10_Q), .b(multiplexer_4_out), .out(adder_2_out));  // open: cin, cout
  // NOT_Gate not_1 is placed but not wired
  Comparator #(.width(4)) comparator_2 (.a(SCORE1_Q), .b(4'b1001), .eq(comparator_2_eq));  // open: gt, lt
  Hex_Digit_Display hex_digit_display_1 (.value(SCORE1_Q));  // open: dp
  Hex_Digit_Display hex_digit_display_2 (.value(SCORE10_Q));  // open: dp
endmodule

module model8 (
  input  [3:0] CAR_COL,
  input  [3:0] OBS_COL,
  input  [3:0] OBS_ROW,
  input  RST,
  output [3:0] ROW_ADDR,
  output [15:0] COL_DATA
);

  wire clock_1_out, comparator_1_eq, comparator_2_eq, decoder_1_p2, decoder_1_p3, decoder_1_p8,
       decoder_1_p11, decoder_1_p12, decoder_1_p13, decoder_1_p14, decoder_1_p15, decoder_1_p16,
       decoder_2_p3, decoder_2_p4, decoder_2_p6, decoder_2_p7;
  wire [0:0] comparator_1_lt;
  wire [3:0] decoder_1_p6;
  wire [15:0] multiplexer_1_p3;
  wire [15:6] multiplexer_2_p3;

  Clock clock_1 (.out(clock_1_out));
  Register #(.width(4)) SCAN_ROW (.D(decoder_1_p6), .en(decoder_1_p8), .clk(ROW_ADDR[0]));  // open: Q, clr
  // Decoder #(.select(4)) decoder_1: pin names not known; wires that end beside it: CAR_COL, decoder_1_p2, decoder_1_p3, ROW_ADDR, 4'b0001, decoder_1_p6, clock_1_out, decoder_1_p8, RST, ROW_ADDR, decoder_1_p11, decoder_1_p12, decoder_1_p13, decoder_1_p14, decoder_1_p15, decoder_1_p16
  // Decoder #(.select(4)) decoder_2: pin names not known; wires that end beside it: decoder_1_p2, decoder_1_p3, decoder_2_p3, decoder_2_p4, OBS_COL, decoder_2_p6, decoder_2_p7, decoder_1_p11, decoder_1_p12, decoder_1_p13, decoder_1_p14, decoder_1_p15, decoder_1_p16
  Adder #(.width(4)) adder_1 (.out(ROW_ADDR));  // open: a, b, cin, cout
  Comparator #(.width(4)) comparator_1 (
    .a(ROW_ADDR), .b({3'b111, comparator_1_lt[0]}), .gt(ROW_ADDR[0]), .eq(comparator_1_eq),
    .lt(comparator_1_lt[0]));
  Comparator #(.width(4)) comparator_2 (.a(ROW_ADDR), .gt(ROW_ADDR[0]), .eq(comparator_2_eq));  // open: b, lt
  DotMatrix #(.inputtype("row"), .matrixcols(1), .matrixrows(16)) ScanBar (.row0(ROW_ADDR[0]));  // open: row1, row2, row3, row4, row5, row6, row7, row8, row9, row10, row11, row12, row13, row14, row15
  // Multiplexer #(.width(16)) multiplexer_1: pin names not known; wires that end beside it: comparator_1_eq, 16'h1, {multiplexer_1_p3[15:10], ROW_ADDR[0], multiplexer_1_p3[8:3], ROW_ADDR[0], multiplexer_1_p3[1:0]}
  // Multiplexer #(.width(16)) multiplexer_2: pin names not known; wires that end beside it: comparator_2_eq, 16'h1, {multiplexer_2_p3, multiplexer_1_p3[15:10]}
  // OR_Gate #(.width(16)) or_1: pin names not known; wires that end beside it: 16'h1, COL_DATA, 16'h1
  // Pins of 1 and 4 bits meet at ROW_ADDR
  // Pins of 1 and 4 bits meet at {3'b111, comparator_1_lt[0]}
  // also tied to VCC on the sheet: comparator_1_lt[0]
endmodule

module Output_system (
);

  LED GRN ();  // open: in
  LED RED ();  // open: in
  // Buzzer buzzer_1: pin names not known
  _7_Segment_Display u_7_segment_display_1 ();  // open: g, f, a, b, e, d, c, dp
  _7_Segment_Display u_7_segment_display_2 ();  // open: g, f, a, b, e, d, c, dp
endmodule
