// Logisim project workdesign.circ as structural Verilog: 19 circuits, main circuit main
module main (
  input  Reset,
  input  [1:0] sel_nd,
  input  SEL
);

  wire button_1_out, button_2_out, clock_1_out, gamestate_1_c_q, gamestate_1_r_q, multiplexer_2_out,
       multiplexer_3_out, test_1_grn, test_1_red;
  wire [1:0] multiplexer_1_out, score_control_1_out_2;
  wire [3:0] module1_1_out_3, test_1_score_1, test_1_score_10;
  wire [6:0] gamestate_1_src;
  wire [15:0] test_1_out_5, test_1_out_6;

  Clock clock_1 (.out(clock_1_out));
  Multiplexer #(.width(2)) multiplexer_1 (
    .in0(score_control_1_out_2), .in1(sel_nd), .out(multiplexer_1_out), .sel(SEL));
  Multiplexer multiplexer_2 (.in0(clock_1_out), .out(multiplexer_2_out), .sel(test_1_red));  // open: in1
  score_control score_control_1 (.game_score(test_1_score_10), .out_2(score_control_1_out_2));
  Button button_1 (.out(button_1_out));
  Button button_2 (.out(button_2_out));
  module1 module1_1 (.clk(multiplexer_2_out), .sel(multiplexer_1_out), .out_3(module1_1_out_3));
  Multiplexer #(.select(2)) multiplexer_3 (
    .in0(module1_1_out_3[0]), .in1(module1_1_out_3[1]), .in2(module1_1_out_3[2]), .in3(module1_1_out_3[3]),
    .out(multiplexer_3_out), .sel(multiplexer_1_out));
  TEST test_1 (
    .Reset(Reset), .Left(button_1_out), .Right(button_2_out), .clk(multiplexer_3_out), .out_5(test_1_out_5),
    .out_6(test_1_out_6), .score_1(test_1_score_1), .score_10(test_1_score_10), .red(test_1_red),
    .grn(test_1_grn));
  GameState gamestate_1 (
    .clk(clock_1_out), .Reset(Reset), .in_3(test_1_grn), .SRC(gamestate_1_src), .C_Q(gamestate_1_c_q),
    .r_q(gamestate_1_r_q));
  Hex_Digit_Display hex_digit_display_1 (.value(test_1_score_10));  // open: dp
  Hex_Digit_Display hex_digit_display_2 (.value(test_1_score_1));  // open: dp
  // DotMatrix #(.inputtype("select"), .matrixcols(16), .matrixrows(16)) dotmatrix_1: pin names not known; wires that end beside it: test_1_out_5, test_1_out_6
  LED led_1 (.in(test_1_red));
  LED led_2 (.in(test_1_grn));
  TTY tty_1 (.data(gamestate_1_src), .clk(gamestate_1_c_q), .clr(gamestate_1_r_q));  // open: we
endmodule

module Input_system (
  input  SPEED0,
  input  SPEED1
);

  Clock CLK ();  // open: out
  Button LEFT ();  // open: out
  Button RIGHT ();  // open: out
  Button START ();  // open: out
  Button RST ();  // open: out
endmodule

module module1 (
  input  clk,
  input  [1:0] sel,
  output [3:0] out_3
);

  wire [3:0] adder_1_out, adder_2_out, adder_3_out, CNT1_q, CNT2_q, CNT3_q;

  Adder #(.width(4)) adder_1 (.a(CNT1_q), .b(4'b0001), .out(adder_1_out));  // open: cin, cout
  Adder #(.width(4)) adder_2 (.a(CNT1_q), .b(CNT1_q), .out(adder_2_out));  // open: cin, cout
  Adder #(.width(4)) adder_3 (.a(CNT2_q), .b(CNT1_q), .out(adder_3_out));  // open: cin, cout
  Register #(.width(4)) CNT1 (.D(adder_1_out), .clk(clk), .Q(CNT1_q));  // open: en, clr
  Register #(.width(4)) CNT2 (.D(adder_2_out), .clk(clk), .Q(CNT2_q));  // open: en, clr
  Register #(.width(4)) CNT3 (.D(adder_3_out), .clk(clk), .Q(CNT3_q));  // open: en, clr
  Multiplexer #(.select(2), .width(4)) multiplexer_1 (
    .in1(CNT1_q), .in2(CNT2_q), .in3(CNT3_q), .out(out_3), .sel(sel));  // open: in0
endmodule

module model2 (
  output [3:0] SRC_PIN
);

  wire clock_1_out;
  wire [3:0] adder_1_out;

  Clock clock_1 (.out(clock_1_out));
  Register #(.width(4)) OBS_SRC (.D(adder_1_out), .clk(clock_1_out), .Q(SRC_PIN));  // open: en, clr
  Adder #(.width(4)) adder_1 (.a(SRC_PIN), .b(4'b0011), .out(adder_1_out));  // open: cin, cout
endmodule

module model3 (
  input  LEFT,
  input  RIGHT,
  input  clk,
  input  Reset,
  output [3:0] car_pos
);

  wire comparator_1_gt, comparator_1_lt, comparator_2_gt, comparator_2_lt, or_1_out, or_2_out;
  wire [1:0] and_2_out;
  wire [3:0] adder_1_out, multiplexer_1_out, multiplexer_2_out;

  Multiplexer #(.select(2), .width(4)) multiplexer_1 (
    .in0(4'b0000), .in1(4'b1111), .in2(4'b0001), .in3(4'b0000), .out(multiplexer_1_out), .sel(and_2_out));
  Adder #(.width(4)) adder_1 (.a(multiplexer_1_out), .b(car_pos), .out(adder_1_out));  // open: cin, cout
  Multiplexer #(.width(4)) multiplexer_2 (.in0(adder_1_out), .in1(4'b1000), .out(multiplexer_2_out), .sel(Reset));
  Register #(.width(4)) register_1 (.D(multiplexer_2_out), .clk(clk), .Q(car_pos));  // open: en, clr
  Comparator #(.width(4)) comparator_1 (
    .a(car_pos), .b(4'b0000), .gt(comparator_1_gt), .lt(comparator_1_lt));  // open: eq
  Comparator #(.width(4)) comparator_2 (
    .a(car_pos), .b(4'b1111), .gt(comparator_2_gt), .lt(comparator_2_lt));  // open: eq
  or or_1 (or_1_out, comparator_1_gt, comparator_1_lt);
  or or_2 (or_2_out, comparator_2_gt, comparator_2_lt);
  and and_1 (and_2_out[1], or_2_out, RIGHT);
  and and_2 (and_2_out[0], LEFT, or_1_out);
endmodule

module model4 (
  input  [3:0] OBS_SRC,
  input  clk,
  input  Reset,
  output [3:0] COL_Q,
  output [3:0] ROW_q,
  output AT_BOTTOM
);

  wire [3:0] adder_1_out;

  Register #(.width(4)) OBS_COL (.D(OBS_SRC), .en(clk), .clk(clk), .Q(COL_Q), .clr(Reset));
  Register #(.width(4)) OBS_ROW (.D(adder_1_out), .en(clk), .clk(clk), .Q(ROW_q), .clr(Reset));
  Adder #(.width(4)) adder_1 (.a(ROW_q), .b(4'b0001), .out(adder_1_out));  // open: cin, cout
  Comparator #(.width(4)) comparator_1 (.a(ROW_q), .b(4'b1111), .eq(AT_BOTTOM));  // open: gt, lt
endmodule

module model5 (
  input  [3:0] X,
  input  [3:0] Y,
  input  At_Botton,
  output hit
);

  wire comparator_1_eq;

  Comparator #(.width(4)) comparator_1 (.a(X), .b(Y), .eq(comparator_1_eq));  // open: gt, lt
  and and_1 (hit, comparator_1_eq, At_Botton);
endmodule

module model6 (
  input  HIT,
  input  clk,
  output RUN,
  output GRN,
  output RED
);

  wire and_1_out, KEEP_out, not_1_out, not_2_out, not_3_out, S0_out, START_out;

  not not_1 (not_1_out, HIT);
  and and_1 (and_1_out, RED, not_1_out);
  and KEEP (KEEP_out, HIT, RED);
  or S0 (S0_out, START_out, and_1_out);
  D_Flip_Flop FF_S1 (.D(KEEP_out), .clk(clk), .Q(GRN));  // open: Qn, preset, reset
  D_Flip_Flop FF_S0 (.D(S0_out), .clk(clk), .Q(RED));  // open: Qn, preset, reset
  not not_2 (not_2_out, GRN);
  not not_3 (not_3_out, RED);
  and START (START_out, not_2_out, not_3_out);

  assign RUN = HIT;
endmodule

module model7 (
  input  clk,
  input  AT_BOTTOM,
  input  HIT,
  input  RUNNING,
  input  reset,
  output [3:0] SCORE1_Q,
  output [3:0] SCORE10_Q
);

  wire and_1_out, comparator_1_eq, comparator_2_eq;
  wire [3:0] adder_1_out, adder_2_out, multiplexer_1_out, multiplexer_2_out, multiplexer_3_out,
       multiplexer_4_out, subtractor_1_out;

  Multiplexer #(.width(4)) multiplexer_1 (
    .in0(subtractor_1_out), .in1(adder_1_out), .out(multiplexer_1_out), .sel(and_1_out));
  Multiplexer #(.width(4)) multiplexer_2 (
    .in0(multiplexer_1_out), .in1(4'b0000), .out(multiplexer_2_out), .sel(comparator_2_eq));
  Multiplexer #(.width(4)) multiplexer_3 (
    .in0(adder_2_out), .in1(4'b0000), .out(multiplexer_3_out), .sel(comparator_1_eq));
  Subtractor #(.width(4)) subtractor_1 (.a(adder_1_out), .b(4'b0001), .out(subtractor_1_out));  // open: bin, bout
  Register #(.width(4)) SCORE1 (.D(multiplexer_2_out), .clk(clk), .Q(SCORE1_Q), .clr(reset));  // open: en
  Register #(.width(4)) SCORE10 (.D(multiplexer_3_out), .clk(clk), .Q(SCORE10_Q), .clr(reset));  // open: en
  Hex_Digit_Display hex_digit_display_1 (.value(SCORE1_Q));  // open: dp
  Adder #(.width(4)) adder_1 (.a(4'b0001), .b(SCORE1_Q), .out(adder_1_out));  // open: cin, cout
  and and_1 (and_1_out, AT_BOTTOM, HIT, RUNNING);
  Adder #(.width(4)) adder_2 (.a(SCORE10_Q), .b(multiplexer_4_out), .out(adder_2_out));  // open: cin, cout
  Multiplexer #(.width(4)) multiplexer_4 (.in0(4'b0000), .in1(4'b0001), .out(multiplexer_4_out), .sel(comparator_2_eq));
  Comparator #(.width(4)) comparator_1 (.a(SCORE10_Q), .b(4'b1001), .eq(comparator_1_eq));  // open: gt, lt
  // NOT_Gate not_1 is placed but not wired
  Comparator #(.width(4)) comparator_2 (.a(SCORE1_Q), .b(4'b1010), .eq(comparator_2_eq));  // open: gt, lt
  Hex_Digit_Display hex_digit_display_2 (.value(SCORE10_Q));  // open: dp
endmodule

module model8 (
  input  CAR,
  input  [3:0] OBS,
  output [3:0] SCAN
);

  wire clock_1_out, comparator_1_gt, comparator_1_lt, decoder_1_out0, decoder_1_out1, decoder_1_out2,
       decoder_1_out3, decoder_1_out4, decoder_1_out5, decoder_1_out6, decoder_1_out7, decoder_1_out8,
       decoder_1_out9, decoder_1_out10, decoder_1_out11, decoder_1_out12, decoder_1_out13, decoder_1_out14,
       decoder_1_out15, or_1_out;
  wire [3:0] adder_1_out, multiplexer_1_out;

  Clock clock_1 (.out(clock_1_out));
  Register #(.width(4)) SCAN_ROW (.D(multiplexer_1_out), .clk(clock_1_out), .Q(SCAN));  // open: en, clr
  Decoder #(.select(4)) decoder_1 (
    .out0(decoder_1_out0), .out1(decoder_1_out1), .out2(decoder_1_out2), .out3(decoder_1_out3),
    .out4(decoder_1_out4), .out5(decoder_1_out5), .out6(decoder_1_out6), .out7(decoder_1_out7),
    .out8(decoder_1_out8), .out9(decoder_1_out9), .out10(decoder_1_out10), .out11(decoder_1_out11),
    .out12(decoder_1_out12), .out13(decoder_1_out13), .out14(decoder_1_out14), .out15(decoder_1_out15),
    .sel(SCAN), .en(CAR));
  DotMatrix #(.inputtype("row"), .matrixcols(1), .matrixrows(16)) LED_Matrix (
    .row0(decoder_1_out0), .row1(decoder_1_out1), .row2(decoder_1_out2), .row3(decoder_1_out3),
    .row4(decoder_1_out4), .row5(decoder_1_out5), .row6(decoder_1_out6), .row7(decoder_1_out7),
    .row8(decoder_1_out8), .row9(decoder_1_out9), .row10(decoder_1_out10), .row11(decoder_1_out11),
    .row12(decoder_1_out12), .row13(decoder_1_out13), .row14(decoder_1_out14), .row15(decoder_1_out15));
  Adder #(.width(4)) adder_1 (.a(SCAN), .b(4'b0001), .out(adder_1_out));  // open: cin, cout
  Comparator #(.width(4)) comparator_1 (
    .a(adder_1_out), .b(4'b1111), .gt(comparator_1_gt), .lt(comparator_1_lt));  // open: eq
  Comparator #(.width(4)) comparator_2 (.a(SCAN), .b(4'b1110));  // open: gt, eq, lt
  Comparator #(.width(4)) comparator_3 (.a(SCAN), .b(4'b1111));  // open: gt, eq, lt
  Comparator #(.width(4)) comparator_4 (.a(SCAN), .b(OBS));  // open: gt, eq, lt
  Multiplexer #(.width(4)) multiplexer_1 (.in0(4'b0000), .in1(adder_1_out), .out(multiplexer_1_out), .sel(or_1_out));
  or or_1 (or_1_out, comparator_1_gt, comparator_1_lt);
endmodule

module Output_system (
);

  LED GRN ();  // open: in
  LED RED ();  // open: in
  // Buzzer buzzer_1: pin names not known
  _7_Segment_Display u_7_segment_display_1 ();  // open: g, f, a, b, e, d, c, dp
  _7_Segment_Display u_7_segment_display_2 ();  // open: g, f, a, b, e, d, c, dp
endmodule

module randon_design (
  input  clk,
  input  reset,
  input  [3:0] goal_row,
  input  [3:0] car_clo,
  input  [3:0] goal_col,
  output [3:0] row_Q,
  output [15:0] out_7
);

  wire comparator_1_eq, comparator_2_eq, not_1_out, not_2_out;
  wire [3:0] subtractor_1_out;
  wire [15:0] decoder_1_out0, decoder_2_out0, multiplexer_1_out, multiplexer_2_out;

  Decoder #(.select(4)) decoder_1 (
    .out0(decoder_1_out0[0]), .out1(decoder_1_out0[1]), .out2(decoder_1_out0[2]), .out3(decoder_1_out0[3]),
    .out4(decoder_1_out0[4]), .out5(decoder_1_out0[5]), .out6(decoder_1_out0[6]), .out7(decoder_1_out0[7]),
    .out8(decoder_1_out0[8]), .out9(decoder_1_out0[9]), .out10(decoder_1_out0[10]),
    .out11(decoder_1_out0[11]), .out12(decoder_1_out0[12]), .out13(decoder_1_out0[13]),
    .out14(decoder_1_out0[14]), .out15(decoder_1_out0[15]), .sel(car_clo));  // open: en
  Register #(.width(4)) SCAN_row (.D(subtractor_1_out), .clk(clk), .Q(row_Q), .clr(reset));  // open: en
  Multiplexer #(.width(16)) multiplexer_1 (
    .in0({16{1'b0}}), .in1(decoder_1_out0), .out(multiplexer_1_out), .sel(not_1_out));
  Subtractor #(.width(4)) subtractor_1 (.a(row_Q), .b(4'b0001), .out(subtractor_1_out));  // open: bin, bout
  Comparator #(.width(4)) comparator_1 (.a(row_Q), .b(4'b1111), .eq(comparator_1_eq));  // open: gt, lt
  Comparator #(.width(4)) comparator_2 (.a(row_Q), .b(goal_row), .eq(comparator_2_eq));  // open: gt, lt
  not not_1 (not_1_out, comparator_2_eq);
  not not_2 (not_2_out, comparator_1_eq);
  Decoder #(.select(4)) decoder_2 (
    .out0(decoder_2_out0[0]), .out1(decoder_2_out0[1]), .out2(decoder_2_out0[2]), .out3(decoder_2_out0[3]),
    .out4(decoder_2_out0[4]), .out5(decoder_2_out0[5]), .out6(decoder_2_out0[6]), .out7(decoder_2_out0[7]),
    .out8(decoder_2_out0[8]), .out9(decoder_2_out0[9]), .out10(decoder_2_out0[10]),
    .out11(decoder_2_out0[11]), .out12(decoder_2_out0[12]), .out13(decoder_2_out0[13]),
    .out14(decoder_2_out0[14]), .out15(decoder_2_out0[15]), .sel(goal_col));  // open: en
  assign out_7 = multiplexer_1_out | multiplexer_2_out;  // OR_Gate or_1, 16 bits wide
  Multiplexer #(.width(16)) multiplexer_2 (
    .in0({16{1'b0}}), .in1(decoder_2_out0), .out(multiplexer_2_out), .sel(not_2_out));
endmodule

module TEST (
  input  Reset,
  input  Left,
  input  Right,
  input  clk,
  output [15:0] out_5,
  output [15:0] out_6,
  output [3:0] score_1,
  output [3:0] score_10,
  output red,
  output grn
);

  wire comparator_1_eq, model5_1_hit, not_1_out, not_2_out, or_1_out;
  wire [3:0] model3_1_car_pos, model4_1_col_q, model4_1_row_q, random_1_out, randon_design_1_row_q;
  wire [15:0] decoder_1_out0, decoder_2_out0;

  or or_1 (or_1_out, comparator_1_eq, Reset);
  Random #(.width(4)) random_1 (.next(decoder_1_out0[15]), .clk(clk), .out(random_1_out));  // open: clr
  model3 model3_1 (.LEFT(Left), .RIGHT(Right), .clk(clk), .Reset(or_1_out), .car_pos(model3_1_car_pos));
  model4 model4_1 (
    .OBS_SRC(random_1_out), .clk(clk), .Reset(or_1_out), .COL_Q(model4_1_col_q), .ROW_q(model4_1_row_q));  // open: AT_BOTTOM
  not not_1 (not_1_out, not_2_out);
  randon_design randon_design_1 (
    .clk(clk), .reset(or_1_out), .goal_row(model4_1_row_q), .car_clo(model3_1_car_pos),
    .goal_col(model4_1_col_q), .row_Q(randon_design_1_row_q), .out_7(out_5));
  Decoder #(.select(4)) decoder_1 (
    .out0(decoder_1_out0[0]), .out1(decoder_1_out0[1]), .out2(decoder_1_out0[2]), .out3(decoder_1_out0[3]),
    .out4(decoder_1_out0[4]), .out5(decoder_1_out0[5]), .out6(decoder_1_out0[6]), .out7(decoder_1_out0[7]),
    .out8(decoder_1_out0[8]), .out9(decoder_1_out0[9]), .out10(decoder_1_out0[10]),
    .out11(decoder_1_out0[11]), .out12(decoder_1_out0[12]), .out13(decoder_1_out0[13]),
    .out14(decoder_1_out0[14]), .out15(decoder_1_out0[15]), .sel(randon_design_1_row_q));  // open: en
  not not_2 (not_2_out, model5_1_hit);
  model5 model5_1 (.X(model3_1_car_pos), .Y(random_1_out), .At_Botton(decoder_1_out0[15]), .hit(model5_1_hit));
  model7 model7_1 (
    .clk(clk), .AT_BOTTOM(decoder_1_out0[15]), .HIT(not_2_out), .RUNNING(decoder_1_out0[15]),
    .reset(or_1_out), .SCORE1_Q(score_1), .SCORE10_Q(score_10));
  model6 model6_1 (.HIT(not_1_out), .clk(clk), .GRN(red), .RED(grn));  // open: RUN
  Decoder #(.select(4)) decoder_2 (
    .out0(decoder_2_out0[0]), .out1(decoder_2_out0[1]), .out2(decoder_2_out0[2]), .out3(decoder_2_out0[3]),
    .out4(decoder_2_out0[4]), .out5(decoder_2_out0[5]), .out6(decoder_2_out0[6]), .out7(decoder_2_out0[7]),
    .out8(decoder_2_out0[8]), .out9(decoder_2_out0[9]), .out10(decoder_2_out0[10]),
    .out11(decoder_2_out0[11]), .out12(decoder_2_out0[12]), .out13(decoder_2_out0[13]),
    .out14(decoder_2_out0[14]), .out15(decoder_2_out0[15]), .sel(4'b0000));  // open: en
  assign out_6 = decoder_2_out0 | decoder_1_out0;  // OR_Gate or_2, 16 bits wide
  Comparator #(.width(1)) comparator_1 (.a(red), .b(1'b1), .eq(comparator_1_eq));  // open: gt, lt
endmodule

module GameState (
  input  clk,
  input  Reset,
  input  in_3,
  output [6:0] SRC,
  output C_Q,
  output r_q
);

  wire [2:0] adder_1_out, adder_2_out, register_1_q, register_2_q;
  wire [6:0] multiplexer_1_out, multiplexer_2_out;

  Multiplexer #(.select(3), .width(7)) multiplexer_1 (
    .in0(7'b1000111), .in1(7'b1100001), .in2(7'b1101101), .in3(7'b1100101), .in4(7'b1001111),
    .in5(7'b1110110), .in6(7'b1100101), .in7(7'b1110010), .out(multiplexer_1_out), .sel(register_1_q));
  Multiplexer #(.select(3), .width(7)) multiplexer_2 (
    .in0(7'b1001001), .in1(7'b1110011), .in2(7'b1000111), .in3(7'b1100001), .in4(7'b1101101),
    .in5(7'b1101001), .in6(7'b1101110), .in7(7'b1100111), .out(multiplexer_2_out), .sel(register_2_q));
  Register #(.width(3)) register_1 (.D(adder_1_out), .clk(clk), .Q(register_1_q), .clr(Reset));  // open: en
  Register #(.width(3)) register_2 (.D(adder_2_out), .clk(clk), .Q(register_2_q), .clr(Reset));  // open: en
  Adder #(.width(3)) adder_1 (.a(register_1_q), .b(3'b001), .out(adder_1_out));  // open: cin, cout
  Adder #(.width(3)) adder_2 (.a(register_2_q), .b(3'b001), .out(adder_2_out));  // open: cin, cout
  Multiplexer #(.width(7)) multiplexer_3 (.in0(multiplexer_1_out), .in1(multiplexer_2_out), .out(SRC), .sel(in_3));

  assign C_Q = clk;
  assign r_q = Reset;
endmodule

module score_control (
  input  [3:0] game_score,
  output [1:0] out_2
);

  wire comparator_3_eq;
  wire [1:0] comparator_1_eq, undriven;

  Comparator #(.width(4)) comparator_1 (.a(game_score), .b(4'b0001), .eq(comparator_1_eq[0]));  // open: gt, lt
  Comparator #(.width(4)) comparator_2 (.a(game_score), .b(4'b0011), .eq(comparator_1_eq[1]));  // open: gt, lt
  Comparator #(.width(4)) comparator_3 (.a(game_score), .b(4'b0110), .eq(comparator_3_eq));  // open: gt, lt
  Multiplexer #(.select(2), .width(2)) multiplexer_1 (
    .in0(2'b11), .in1(2'b10), .in2(2'b01), .in3(undriven), .out(out_2), .sel(comparator_1_eq));
endmodule

module col_control (
  input  LEFT,
  input  RIGHT,
  input  CLK,
  input  RESET,
  output [15:0] ZERO,
  output [15:0] out_6,
  output [15:0] out_7,
  output [15:0] out_8,
  output [15:0] out_9,
  output [15:0] out_10,
  output [15:0] out_11,
  output [15:0] out_12,
  output [15:0] out_13,
  output [15:0] out_14,
  output [15:0] out_15,
  output [15:0] out_16,
  output [15:0] out_17,
  output [15:0] out_18,
  output [15:0] out_19,
  output [15:0] out_20,
  output [3:0] CAR_COL
);

  wire decoder_2_out0, decoder_2_out1, decoder_2_out2, decoder_2_out3, decoder_2_out4, decoder_2_out5,
       decoder_2_out6, decoder_2_out7, decoder_2_out8, decoder_2_out9, decoder_2_out10, decoder_2_out11,
       decoder_2_out12, decoder_2_out13, decoder_2_out14, decoder_2_out15;
  wire [15:0] decoder_1_out0;

  Decoder #(.select(4)) decoder_1 (
    .out0(decoder_1_out0[0]), .out1(decoder_1_out0[1]), .out2(decoder_1_out0[2]), .out3(decoder_1_out0[3]),
    .out4(decoder_1_out0[4]), .out5(decoder_1_out0[5]), .out6(decoder_1_out0[6]), .out7(decoder_1_out0[7]),
    .out8(decoder_1_out0[8]), .out9(decoder_1_out0[9]), .out10(decoder_1_out0[10]),
    .out11(decoder_1_out0[11]), .out12(decoder_1_out0[12]), .out13(decoder_1_out0[13]),
    .out14(decoder_1_out0[14]), .out15(decoder_1_out0[15]), .sel(4'b0000));  // open: en
  model3 model3_1 (.LEFT(LEFT), .RIGHT(RIGHT), .clk(CLK), .Reset(RESET), .car_pos(CAR_COL));
  Multiplexer #(.width(16)) multiplexer_1 (.in0({16{1'b0}}), .in1(decoder_1_out0), .out(ZERO), .sel(decoder_2_out0));
  Multiplexer #(.width(16)) multiplexer_2 (.in0({16{1'b0}}), .in1(decoder_1_out0), .out(out_13), .sel(decoder_2_out8));
  Multiplexer #(.width(16)) multiplexer_3 (.in0({16{1'b0}}), .in1(decoder_1_out0), .out(out_6), .sel(decoder_2_out1));
  Multiplexer #(.width(16)) multiplexer_4 (.in0({16{1'b0}}), .in1(decoder_1_out0), .out(out_14), .sel(decoder_2_out9));
  Multiplexer #(.width(16)) multiplexer_5 (.in0({16{1'b0}}), .in1(decoder_1_out0), .out(out_7), .sel(decoder_2_out2));
  Decoder #(.select(4)) decoder_2 (
    .out0(decoder_2_out0), .out1(decoder_2_out1), .out2(decoder_2_out2), .out3(decoder_2_out3),
    .out4(decoder_2_out4), .out5(decoder_2_out5), .out6(decoder_2_out6), .out7(decoder_2_out7),
    .out8(decoder_2_out8), .out9(decoder_2_out9), .out10(decoder_2_out10), .out11(decoder_2_out11),
    .out12(decoder_2_out12), .out13(decoder_2_out13), .out14(decoder_2_out14), .out15(decoder_2_out15),
    .sel(CAR_COL));  // open: en
  Multiplexer #(.width(16)) multiplexer_6 (.in0({16{1'b0}}), .in1(decoder_1_out0), .out(out_15), .sel(decoder_2_out10));
  Multiplexer #(.width(16)) multiplexer_7 (.in0({16{1'b0}}), .in1(decoder_1_out0), .out(out_8), .sel(decoder_2_out3));
  Multiplexer #(.width(16)) multiplexer_8 (.in0({16{1'b0}}), .in1(decoder_1_out0), .out(out_9), .sel(decoder_2_out4));
  Multiplexer #(.width(16)) multiplexer_9 (.in0({16{1'b0}}), .in1(decoder_1_out0), .out(out_16), .sel(decoder_2_out11));
  Multiplexer #(.width(16)) multiplexer_10 (
    .in0({16{1'b0}}), .in1(decoder_1_out0), .out(out_17), .sel(decoder_2_out12));
  Multiplexer #(.width(16)) multiplexer_11 (.in0({16{1'b0}}), .in1(decoder_1_out0), .out(out_10), .sel(decoder_2_out5));
  Multiplexer #(.width(16)) multiplexer_12 (
    .in0({16{1'b0}}), .in1(decoder_1_out0), .out(out_18), .sel(decoder_2_out13));
  Multiplexer #(.width(16)) multiplexer_13 (.in0({16{1'b0}}), .in1(decoder_1_out0), .out(out_11), .sel(decoder_2_out6));
  Multiplexer #(.width(16)) multiplexer_14 (
    .in0({16{1'b0}}), .in1(decoder_1_out0), .out(out_19), .sel(decoder_2_out14));
  Multiplexer #(.width(16)) multiplexer_15 (.in0({16{1'b0}}), .in1(decoder_1_out0), .out(out_12), .sel(decoder_2_out7));
  Multiplexer #(.width(16)) multiplexer_16 (
    .in0({16{1'b0}}), .in1(decoder_1_out0), .out(out_20), .sel(decoder_2_out15));
endmodule

module bar_control (
  input  CLK,
  input  RESET,
  output [15:0] ZERO,
  output [15:0] out_4,
  output [15:0] out_5,
  output [15:0] out_6,
  output [15:0] out_7,
  output [15:0] out_8,
  output [15:0] out_9,
  output [15:0] out_10,
  output [15:0] out_11,
  output [15:0] out_12,
  output [15:0] out_13,
  output [15:0] out_14,
  output [15:0] out_15,
  output [15:0] out_16,
  output [15:0] out_17,
  output [15:0] out_18,
  output RECYCLE,
  output [3:0] BAR_COL
);

  wire decoder_2_out0, decoder_2_out1, decoder_2_out2, decoder_2_out3, decoder_2_out4, decoder_2_out5,
       decoder_2_out6, decoder_2_out7, decoder_2_out8, decoder_2_out9, decoder_2_out10, decoder_2_out11,
       decoder_2_out12, decoder_2_out13, decoder_2_out14, decoder_2_out15;
  wire [3:0] adder_1_out, register_1_q;
  wire [15:1] decoder_1_out14;

  Register #(.width(4)) register_1 (.D(adder_1_out), .clk(CLK), .Q(register_1_q), .clr(RESET));  // open: en
  Adder #(.width(4)) adder_1 (.a(register_1_q), .b(4'b0001), .out(adder_1_out));  // open: cin, cout
  Random #(.width(4)) random_1 (.next(RECYCLE), .clk(CLK), .out(BAR_COL));  // open: clr
  Decoder #(.select(4)) decoder_1 (
    .out0(decoder_1_out14[15]), .out1(decoder_1_out14[14]), .out2(decoder_1_out14[13]),
    .out3(decoder_1_out14[12]), .out4(decoder_1_out14[11]), .out5(decoder_1_out14[10]),
    .out6(decoder_1_out14[9]), .out7(decoder_1_out14[8]), .out8(decoder_1_out14[7]),
    .out9(decoder_1_out14[6]), .out10(decoder_1_out14[5]), .out11(decoder_1_out14[4]),
    .out12(decoder_1_out14[3]), .out13(decoder_1_out14[2]), .out14(decoder_1_out14[1]), .out15(RECYCLE),
    .sel(adder_1_out));  // open: en
  Multiplexer #(.width(16)) multiplexer_1 (
    .in0({16{1'b0}}), .in1({decoder_1_out14, RECYCLE}), .out(ZERO), .sel(decoder_2_out0));
  Multiplexer #(.width(16)) multiplexer_2 (
    .in0({16{1'b0}}), .in1({decoder_1_out14, RECYCLE}), .out(out_11), .sel(decoder_2_out8));
  Multiplexer #(.width(16)) multiplexer_3 (
    .in0({16{1'b0}}), .in1({decoder_1_out14, RECYCLE}), .out(out_4), .sel(decoder_2_out1));
  Multiplexer #(.width(16)) multiplexer_4 (
    .in0({16{1'b0}}), .in1({decoder_1_out14, RECYCLE}), .out(out_5), .sel(decoder_2_out2));
  Decoder #(.select(4)) decoder_2 (
    .out0(decoder_2_out0), .out1(decoder_2_out1), .out2(decoder_2_out2), .out3(decoder_2_out3),
    .out4(decoder_2_out4), .out5(decoder_2_out5), .out6(decoder_2_out6), .out7(decoder_2_out7),
    .out8(decoder_2_out8), .out9(decoder_2_out9), .out10(decoder_2_out10), .out11(decoder_2_out11),
    .out12(decoder_2_out12), .out13(decoder_2_out13), .out14(decoder_2_out14), .out15(decoder_2_out15),
    .sel(BAR_COL));  // open: en
  Multiplexer #(.width(16)) multiplexer_5 (
    .in0({16{1'b0}}), .in1({decoder_1_out14, RECYCLE}), .out(out_12), .sel(decoder_2_out9));
  Multiplexer #(.width(16)) multiplexer_6 (
    .in0({16{1'b0}}), .in1({decoder_1_out14, RECYCLE}), .out(out_13), .sel(decoder_2_out10));
  Multiplexer #(.width(16)) multiplexer_7 (
    .in0({16{1'b0}}), .in1({decoder_1_out14, RECYCLE}), .out(out_6), .sel(decoder_2_out3));
  Multiplexer #(.width(16)) multiplexer_8 (
    .in0({16{1'b0}}), .in1({decoder_1_out14, RECYCLE}), .out(out_14), .sel(decoder_2_out11));
  Multiplexer #(.width(16)) multiplexer_9 (
    .in0({16{1'b0}}), .in1({decoder_1_out14, RECYCLE}), .out(out_7), .sel(decoder_2_out4));
  Multiplexer #(.width(16)) multiplexer_10 (
    .in0({16{1'b0}}), .in1({decoder_1_out14, RECYCLE}), .out(out_8), .sel(decoder_2_out5));
  Multiplexer #(.width(16)) multiplexer_11 (
    .in0({16{1'b0}}), .in1({decoder_1_out14, RECYCLE}), .out(out_15), .sel(decoder_2_out12));
  Multiplexer #(.width(16)) multiplexer_12 (
    .in0({16{1'b0}}), .in1({decoder_1_out14, RECYCLE}), .out(out_16), .sel(decoder_2_out13));
  Multiplexer #(.width(16)) multiplexer_13 (
    .in0({16{1'b0}}), .in1({decoder_1_out14, RECYCLE}), .out(out_9), .sel(decoder_2_out6));
  Multiplexer #(.width(16)) multiplexer_14 (
    .in0({16{1'b0}}), .in1({decoder_1_out14, RECYCLE}), .out(out_17), .sel(decoder_2_out14));
  Multiplexer #(.width(16)) multiplexer_15 (
    .in0({16{1'b0}}), .in1({decoder_1_out14, RECYCLE}), .out(out_10), .sel(decoder_2_out7));
  Multiplexer #(.width(16)) multiplexer_16 (
    .in0({16{1'b0}}), .in1({decoder_1_out14, RECYCLE}), .out(out_18), .sel(decoder_2_out15));
endmodule

module FINAL_DESIGN (
  input  RESET,
  input  [1:0] SEL,
  input  in_3
);

  wire clock_1_out, gamestate_1_c_q, gamestate_1_r_q, LEFT_out, model6_1_grn, model6_1_red, model6_1_run,
       multiplexer_2_out, multiplexer_3_out, not_1_out, or_1_out, RIGHT_out, screen_1_hit, screen_1_recyclie;
  wire [1:0] multiplexer_1_out, score_control_1_out_2;
  wire [3:0] decoder_1_out0, model7_1_score1_q, model7_1_score10_q, module1_1_out_3;
  wire [6:0] gamestate_1_src;
  wire [15:0] screen_1_out_5, screen_1_out_6, screen_1_out_7, screen_1_out_8, screen_1_out_9,
       screen_1_out_10, screen_1_out_11, screen_1_out_12, screen_1_out_13, screen_1_out_14, screen_1_out_15,
       screen_1_out_16, screen_1_out_17, screen_1_out_18, screen_1_out_19, screen_1_out_20;

  Clock clock_1 (.out(clock_1_out));
  Multiplexer #(.width(2)) multiplexer_1 (.in0(score_control_1_out_2), .in1(SEL), .out(multiplexer_1_out), .sel(in_3));
  Multiplexer multiplexer_2 (.in0(clock_1_out), .in1(RESET), .out(multiplexer_2_out), .sel(model6_1_grn));
  Decoder #(.select(2)) decoder_1 (
    .out0(decoder_1_out0[0]), .out1(decoder_1_out0[1]), .out2(decoder_1_out0[2]), .out3(decoder_1_out0[3]),
    .sel(multiplexer_1_out));  // open: en
  Hex_Digit_Display DIFFICULTY_SEL (.value(decoder_1_out0));  // open: dp
  score_control score_control_1 (.game_score(model7_1_score10_q), .out_2(score_control_1_out_2));
  module1 module1_1 (.clk(multiplexer_2_out), .sel(multiplexer_1_out), .out_3(module1_1_out_3));
  Multiplexer #(.select(2)) multiplexer_3 (
    .in0(module1_1_out_3[0]), .in1(module1_1_out_3[1]), .in2(module1_1_out_3[2]), .in3(module1_1_out_3[3]),
    .out(multiplexer_3_out), .sel(multiplexer_1_out));
  Button LEFT (.out(LEFT_out));
  or or_1 (or_1_out, RESET, model6_1_grn);
  Button RIGHT (.out(RIGHT_out));
  SCREEN screen_1 (
    .LEFT(LEFT_out), .RIGHT(RIGHT_out), .CLK(multiplexer_3_out), .RESET(or_1_out), .out_5(screen_1_out_5),
    .out_6(screen_1_out_6), .out_7(screen_1_out_7), .out_8(screen_1_out_8), .out_9(screen_1_out_9),
    .out_10(screen_1_out_10), .out_11(screen_1_out_11), .out_12(screen_1_out_12), .out_13(screen_1_out_13),
    .out_14(screen_1_out_14), .out_15(screen_1_out_15), .out_16(screen_1_out_16), .out_17(screen_1_out_17),
    .out_18(screen_1_out_18), .out_19(screen_1_out_19), .out_20(screen_1_out_20),
    .RECYCLIE(screen_1_recyclie), .HIT(screen_1_hit));
  DotMatrix #(.matrixcols(16), .matrixrows(16)) dotmatrix_1 (
    .col0(screen_1_out_5), .col1(screen_1_out_6), .col2(screen_1_out_7), .col3(screen_1_out_8),
    .col4(screen_1_out_9), .col5(screen_1_out_10), .col6(screen_1_out_11), .col7(screen_1_out_12),
    .col8(screen_1_out_13), .col9(screen_1_out_14), .col10(screen_1_out_15), .col11(screen_1_out_16),
    .col12(screen_1_out_17), .col13(screen_1_out_18), .col14(screen_1_out_19), .col15(screen_1_out_20));
  not not_1 (not_1_out, screen_1_hit);
  GameState gamestate_1 (
    .clk(clock_1_out), .Reset(RESET), .in_3(model6_1_red), .SRC(gamestate_1_src), .C_Q(gamestate_1_c_q),
    .r_q(gamestate_1_r_q));
  model7 model7_1 (
    .clk(multiplexer_3_out), .AT_BOTTOM(screen_1_recyclie), .HIT(screen_1_hit), .RUNNING(model6_1_red),
    .reset(or_1_out), .SCORE1_Q(model7_1_score1_q), .SCORE10_Q(model7_1_score10_q));
  model6 model6_1 (
    .HIT(not_1_out), .clk(multiplexer_3_out), .RUN(model6_1_run), .GRN(model6_1_grn), .RED(model6_1_red));
  LED led_1 (.in(model6_1_grn));
  LED led_2 (.in(model6_1_red));
  Hex_Digit_Display hex_digit_display_1 (.value(model7_1_score10_q));  // open: dp
  TTY tty_1 (.data(gamestate_1_src), .clk(gamestate_1_c_q), .clr(gamestate_1_r_q));  // open: we
  Hex_Digit_Display hex_digit_display_2 (.value(model7_1_score1_q));  // open: dp
endmodule

module SCREEN (
  input  LEFT,
  input  RIGHT,
  input  CLK,
  input  RESET,
  output [15:0] out_5,
  output [15:0] out_6,
  output [15:0] out_7,
  output [15:0] out_8,
  output [15:0] out_9,
  output [15:0] out_10,
  output [15:0] out_11,
  output [15:0] out_12,
  output [15:0] out_13,
  output [15:0] out_14,
  output [15:0] out_15,
  output [15:0] out_16,
  output [15:0] out_17,
  output [15:0] out_18,
  output [15:0] out_19,
  output [15:0] out_20,
  output RECYCLIE,
  output HIT
);

  wire model5_1_hit;
  wire [3:0] bar_control_1_bar_col, col_control_1_car_col;
  wire [15:0] bar_control_1_out_4, bar_control_1_out_5, bar_control_1_out_6, bar_control_1_out_7,
       bar_control_1_out_8, bar_control_1_out_9, bar_control_1_out_10, bar_control_1_out_11,
       bar_control_1_out_12, bar_control_1_out_13, bar_control_1_out_14, bar_control_1_out_15,
       bar_control_1_out_16, bar_control_1_out_17, bar_control_1_out_18, bar_control_1_zero,
       col_control_1_out_6, col_control_1_out_7, col_control_1_out_8, col_control_1_out_9,
       col_control_1_out_10, col_control_1_out_11, col_control_1_out_12, col_control_1_out_13,
       col_control_1_out_14, col_control_1_out_15, col_control_1_out_16, col_control_1_out_17,
       col_control_1_out_18, col_control_1_out_19, col_control_1_out_20, col_control_1_zero;

  col_control col_control_1 (
    .LEFT(LEFT), .RIGHT(RIGHT), .CLK(CLK), .RESET(RESET), .ZERO(col_control_1_zero),
    .out_6(col_control_1_out_6), .out_7(col_control_1_out_7), .out_8(col_control_1_out_8),
    .out_9(col_control_1_out_9), .out_10(col_control_1_out_10), .out_11(col_control_1_out_11),
    .out_12(col_control_1_out_12), .out_13(col_control_1_out_13), .out_14(col_control_1_out_14),
    .out_15(col_control_1_out_15), .out_16(col_control_1_out_16), .out_17(col_control_1_out_17),
    .out_18(col_control_1_out_18), .out_19(col_control_1_out_19), .out_20(col_control_1_out_20),
    .CAR_COL(col_control_1_car_col));
  bar_control bar_control_1 (
    .CLK(CLK), .RESET(RESET), .ZERO(bar_control_1_zero), .out_4(bar_control_1_out_4),
    .out_5(bar_control_1_out_5), .out_6(bar_control_1_out_6), .out_7(bar_control_1_out_7),
    .out_8(bar_control_1_out_8), .out_9(bar_control_1_out_9), .out_10(bar_control_1_out_10),
    .out_11(bar_control_1_out_11), .out_12(bar_control_1_out_12), .out_13(bar_control_1_out_13),
    .out_14(bar_control_1_out_14), .out_15(bar_control_1_out_15), .out_16(bar_control_1_out_16),
    .out_17(bar_control_1_out_17), .out_18(bar_control_1_out_18), .RECYCLE(RECYCLIE),
    .BAR_COL(bar_control_1_bar_col));
  assign out_7 = col_control_1_out_7 | bar_control_1_out_5;  // OR_Gate or_1, 16 bits wide
  assign out_5 = col_control_1_zero | bar_control_1_zero;  // OR_Gate or_2, 16 bits wide
  assign out_6 = col_control_1_out_6 | bar_control_1_out_4;  // OR_Gate or_3, 16 bits wide
  assign out_10 = col_control_1_out_10 | bar_control_1_out_8;  // OR_Gate or_4, 16 bits wide
  assign out_8 = col_control_1_out_8 | bar_control_1_out_6;  // OR_Gate or_5, 16 bits wide
  assign out_9 = col_control_1_out_9 | bar_control_1_out_7;  // OR_Gate or_6, 16 bits wide
  assign out_16 = col_control_1_out_16 | bar_control_1_out_14;  // OR_Gate or_7, 16 bits wide
  assign out_14 = col_control_1_out_14 | bar_control_1_out_12;  // OR_Gate or_8, 16 bits wide
  assign out_15 = col_control_1_out_15 | bar_control_1_out_13;  // OR_Gate or_9, 16 bits wide
  assign out_11 = col_control_1_out_11 | bar_control_1_out_9;  // OR_Gate or_10, 16 bits wide
  assign out_13 = col_control_1_out_13 | bar_control_1_out_11;  // OR_Gate or_11, 16 bits wide
  assign out_12 = col_control_1_out_12 | bar_control_1_out_10;  // OR_Gate or_12, 16 bits wide
  assign out_17 = col_control_1_out_17 | bar_control_1_out_15;  // OR_Gate or_13, 16 bits wide
  model5 model5_1 (.X(col_control_1_car_col), .Y(bar_control_1_bar_col), .At_Botton(RECYCLIE), .hit(model5_1_hit));
  assign out_18 = col_control_1_out_18 | bar_control_1_out_16;  // OR_Gate or_14, 16 bits wide
  assign out_19 = col_control_1_out_19 | bar_control_1_out_17;  // OR_Gate or_15, 16 bits wide
  assign out_20 = col_control_1_out_20 | bar_control_1_out_18;  // OR_Gate or_16, 16 bits wide
  not not_1 (HIT, model5_1_hit);
endmodule
